// Logisim project Gshare- Finished.circ as structural Verilog: 5 circuits, main circuit main
module main (
);

  wire Clock, Correct, CorrectPred, Done, gsharepredictor_1_takebranch, inputgen_1_branchtaken,
       inputgen_1_isbranch, IsPredBranchCorrect, IsPredCorrect, not_1_out;
  wire [31:0] CorrectPredBranch, gsharepredictor_1_predbranchdest, inputgen_1_branchdestaddress,
       inputgen_1_predpc, inputgen_1_updatepc;

  InputGen inputgen_1 (
    .Clock(Clock), .PredPC(inputgen_1_predpc), .UpdatePC(inputgen_1_updatepc),
    .IsBranch(inputgen_1_isbranch), .BranchTaken(inputgen_1_branchtaken),
    .BranchDestAddress(inputgen_1_branchdestaddress));
  GsharePredictor gsharepredictor_1 (
    .PredPC(inputgen_1_predpc), .UpdatePC(inputgen_1_updatepc), .IsBranch(inputgen_1_isbranch),
    .BranchTaken(inputgen_1_branchtaken), .BranchDestAddr(inputgen_1_branchdestaddress), .Clock(Clock),
    .TakeBranch(gsharepredictor_1_takebranch), .PredBranchDest(gsharepredictor_1_predbranchdest));
  Clock clock_1 (.out(Clock));
  // Probe on CorrectPredBranch
  Test test_1 (
    .TakeBranch(gsharepredictor_1_takebranch), .PredBranchAddress(gsharepredictor_1_predbranchdest),
    .Clock(Clock), .IsPredCorrect(IsPredCorrect), .CorrectPred(CorrectPred),
    .IsPredBranchCorrect(IsPredBranchCorrect), .CorrectPredBranch(CorrectPredBranch), .Correct(Correct),
    .Done(Done));
  not not_1 (not_1_out, Done);
  Shift_Register #(.length(28)) shift_register_1 (
    .shift(not_1_out), .in(Correct), .clk(Clock));  // open: out, load, clr, d0, q0, d1, q1, d2, q2, d3, q3, d4, q4, d5, q5, d6, q6, d7, q7, d8, q8, d9, q9, d10, q10, d11, q11, d12, q12, d13, q13, d14, q14, d15, q15, d16, q16, d17, q17, d18, q18, d19, q19, d20, q20, d21, q21, d22, q22, d23, q23, d24, q24, d25, q25, d26, q26, d27, q27
  // Probe on IsPredCorrect
  // Probe on CorrectPred
  // Probe on IsPredBranchCorrect
  // Probe on CorrectPredBranch
  // Probe on Correct
  // Probe on Done
endmodule

module GsharePredictor (
  input  [31:0] PredPC,
  input  [31:0] UpdatePC,
  input  IsBranch,
  input  BranchTaken,
  input  [31:0] BranchDestAddr,
  input  Clock,
  output TakeBranch,
  output [31:0] PredBranchDest
);

  wire and_1_out, and_2_out, and_3_out, and_6_out, and_7_out, and_10_out, and_11_out, and_12_out, and_13_out,
       and_14_out, and_17_out, and_18_out, and_19_out, and_20_out, and_23_out, and_25_out, and_26_out,
       and_27_out, and_30_out, and_31_out, comparator_1_eq, comparator_2_eq, comparator_3_eq,
       comparator_4_eq, comparator_5_eq, comparator_6_eq, comparator_7_eq, comparator_7_lt, comparator_8_eq,
       comparator_9_eq, comparator_10_eq, comparator_11_eq, comparator_12_eq, mux0, mux1, mux2, mux3,
       or_1_out, or_2_out, or_4_out, or_5_out, or_7_out, or_8_out, or_10_out, or_11_out, undriven,
       undriven_2, undriven_3;
  wire [0:0] and_4_out, and_5_out, and_8_out, and_9_out, and_15_out, and_16_out, and_28_out, and_29_out;
  wire [1:0] counter_1_q, counter_2_q, counter_3_q, counter_4_q, index, or_3_out, or_6_out, or_9_out,
       or_12_out, shift_register_1_q0;
  wire [31:0] PC_2_q, PC_3_q, PC_4_q, PC_q, register_1_q, register_2_q, register_3_q, register_4_q;

  Shift_Register #(.length(2)) shift_register_1 (
    .shift(IsBranch), .in(BranchTaken), .clk(Clock), .q0(shift_register_1_q0[0]), .q1(shift_register_1_q0[1]));  // open: out, load, clr, d0, d1
  assign index = UpdatePC[1:0] ^ shift_register_1_q0;  // XOR_Gate xor_1, 2 bits wide
  // Probe on index
  Register #(.width(32)) PC (.D(UpdatePC), .Q(PC_q), .clk(Clock));  // open: en, clr
  Register #(.width(32)) PC_2 (.D(UpdatePC), .Q(PC_2_q), .clk(Clock));  // open: en, clr
  Comparator #(.width(2), .mode("unsigned")) comparator_1 (.a(index), .b(2'b10), .eq(comparator_1_eq));  // open: gt, lt
  Comparator #(.width(32), .mode("unsigned")) comparator_2 (
    .a(PC_q), .b(UpdatePC), .eq(comparator_2_eq));  // open: gt, lt
  Comparator #(.width(2), .mode("unsigned")) comparator_3 (.a(index), .b(2'b01), .eq(comparator_3_eq));  // open: gt, lt
  Comparator #(.width(32), .mode("unsigned")) comparator_4 (
    .a(PC_2_q), .b(UpdatePC), .eq(comparator_4_eq));  // open: gt, lt
  Register #(.width(32)) PC_3 (.D(UpdatePC), .Q(PC_3_q), .clk(Clock));  // open: en, clr
  and and_1 (and_1_out, comparator_1_eq, comparator_1_eq);
  and and_2 (and_2_out, comparator_2_eq, comparator_1_eq, BranchTaken);
  and and_3 (and_3_out, comparator_2_eq, comparator_1_eq, ~BranchTaken);  // AND_Gate
  and and_4 (and_4_out[0], ~comparator_2_eq, comparator_1_eq, ~BranchTaken);  // AND_Gate
  and and_5 (and_5_out[0], ~comparator_2_eq, comparator_1_eq, BranchTaken);  // AND_Gate
  and and_6 (and_6_out, comparator_4_eq, comparator_3_eq, BranchTaken);
  and and_7 (and_7_out, comparator_4_eq, comparator_3_eq, ~BranchTaken);  // AND_Gate
  and and_8 (and_8_out[0], ~comparator_4_eq, comparator_3_eq, ~BranchTaken);  // AND_Gate
  and and_9 (and_9_out[0], ~comparator_4_eq, comparator_3_eq, BranchTaken);  // AND_Gate
  Comparator #(.width(2), .mode("unsigned")) comparator_5 (.a(index), .b(2'b00), .eq(comparator_5_eq));  // open: gt, lt
  Comparator #(.width(32), .mode("unsigned")) comparator_6 (
    .a(PC_3_q), .b(UpdatePC), .eq(comparator_6_eq));  // open: gt, lt
  Register #(.width(32)) register_1 (.D(BranchDestAddr), .en(and_1_out), .Q(register_1_q), .clk(Clock));  // open: clr
  or or_1 (or_1_out, and_2_out, and_3_out);
  and and_10 (and_10_out, comparator_3_eq, comparator_3_eq);
  and and_11 (and_11_out, comparator_1_eq, or_2_out);
  or or_2 (or_2_out, and_3_out, ~and_2_out);  // OR_Gate
  assign or_3_out = {1'b0, and_4_out[0]} | {1'b0, and_5_out[0]};  // OR_Gate or_3, 2 bits wide
  // Probe on undriven
  Register #(.width(32)) register_2 (.D(BranchDestAddr), .en(and_10_out), .Q(register_2_q), .clk(Clock));  // open: clr
  or or_4 (or_4_out, and_7_out, ~and_6_out);  // OR_Gate
  or or_5 (or_5_out, and_6_out, and_7_out);
  and and_12 (and_12_out, comparator_5_eq, comparator_5_eq);
  and and_13 (and_13_out, comparator_6_eq, comparator_5_eq, BranchTaken);
  and and_14 (and_14_out, comparator_6_eq, comparator_5_eq, ~BranchTaken);  // AND_Gate
  and and_15 (and_15_out[0], ~comparator_6_eq, comparator_5_eq, ~BranchTaken);  // AND_Gate
  and and_16 (and_16_out[0], ~comparator_6_eq, comparator_5_eq, BranchTaken);  // AND_Gate
  and and_17 (and_17_out, comparator_3_eq, or_4_out);
  assign or_6_out = {1'b0, and_8_out[0]} | {1'b0, and_9_out[0]};  // OR_Gate or_6, 2 bits wide
  Register #(.width(32)) register_3 (.D(BranchDestAddr), .en(and_12_out), .Q(register_3_q), .clk(Clock));  // open: clr
  or or_7 (or_7_out, and_14_out, ~and_13_out);  // OR_Gate
  or or_8 (or_8_out, and_13_out, and_14_out);
  Counter #(.width(2), .max('h3), .ongoal("stay")) counter_1 (
    .load(and_11_out), .D(or_3_out), .count(or_1_out), .Q(counter_1_q), .clk(Clock));  // open: carry, clr
  // Probe on or_3_out
  Counter #(.width(2), .max('h3), .ongoal("stay")) counter_2 (
    .load(and_17_out), .D(or_6_out), .count(or_5_out), .Q(counter_2_q), .clk(Clock));  // open: carry, clr
  and and_18 (and_18_out, comparator_5_eq, or_7_out);
  assign or_9_out = {1'b0, and_15_out[0]} | {1'b0, and_16_out[0]};  // OR_Gate or_9, 2 bits wide
  // Probe on or_6_out
  Multiplexer #(.select(2), .enable("false")) multiplexer_1 (
    .in0(mux0), .in1(mux1), .in2(mux2), .in3(mux3), .out(TakeBranch), .sel(index));
  // Probe on undriven_2
  and and_19 (and_19_out, counter_1_q[1], BranchTaken);
  // Probe on counter_2_q[1]
  and and_20 (and_20_out, counter_2_q[1], BranchTaken);
  Counter #(.width(2), .max('h3), .ongoal("stay")) counter_3 (
    .load(and_18_out), .D(or_9_out), .count(or_8_out), .Q(counter_3_q), .clk(Clock));  // open: carry, clr
  // Probe on or_9_out
  Multiplexer #(.select(2), .width(32), .enable("false")) multiplexer_2 (
    .in0(register_3_q), .in1(register_2_q), .in2(register_1_q), .in3(register_4_q), .out(PredBranchDest),
    .sel(index));
  and and_21 (mux2, comparator_9_eq, and_19_out);
  and and_22 (mux1, comparator_7_eq, and_20_out);
  // Probe on counter_3_q[1]
  and and_23 (and_23_out, counter_3_q[1], BranchTaken);
  Comparator #(.width(2), .mode("unsigned")) comparator_7 (
    .a(index), .b(2'b01), .eq(comparator_7_eq), .lt(comparator_7_lt));  // open: gt
  Comparator #(.width(2), .mode("unsigned")) comparator_8 (.a(index), .b(2'b00), .eq(comparator_8_eq));  // open: gt, lt
  and and_24 (mux0, comparator_8_eq, and_23_out);
  Comparator #(.width(2), .mode("unsigned")) comparator_9 (.a(index), .b(2'b10), .eq(comparator_9_eq));  // open: gt, lt
  Register #(.width(32)) PC_4 (.D(UpdatePC), .Q(PC_4_q), .clk(Clock));  // open: en, clr
  Comparator #(.width(2), .mode("unsigned")) comparator_10 (
    .a(index), .b(2'b11), .eq(comparator_10_eq));  // open: gt, lt
  Comparator #(.width(32), .mode("unsigned")) comparator_11 (
    .a(PC_4_q), .b(UpdatePC), .eq(comparator_11_eq));  // open: gt, lt
  and and_25 (and_25_out, comparator_10_eq, comparator_10_eq);
  and and_26 (and_26_out, comparator_11_eq, comparator_10_eq, BranchTaken);
  and and_27 (and_27_out, comparator_11_eq, comparator_10_eq, ~BranchTaken);  // AND_Gate
  and and_28 (and_28_out[0], ~comparator_11_eq, comparator_10_eq, ~BranchTaken);  // AND_Gate
  and and_29 (and_29_out[0], ~comparator_11_eq, comparator_10_eq, BranchTaken);  // AND_Gate
  Register #(.width(32)) register_4 (.D(BranchDestAddr), .en(and_25_out), .Q(register_4_q), .clk(Clock));  // open: clr
  or or_10 (or_10_out, and_27_out, ~and_26_out);  // OR_Gate
  or or_11 (or_11_out, and_26_out, and_27_out);
  and and_30 (and_30_out, comparator_10_eq, or_10_out);
  assign or_12_out = {1'b0, and_28_out[0]} | {1'b0, and_29_out[0]};  // OR_Gate or_12, 2 bits wide
  Counter #(.width(2), .max('h3), .ongoal("stay")) counter_4 (
    .load(and_30_out), .D(or_12_out), .count(or_11_out), .Q(counter_4_q), .clk(Clock));  // open: carry, clr
  // Probe on or_12_out
  // Probe on undriven_3
  and and_31 (and_31_out, counter_4_q[1], BranchTaken);
  and and_32 (mux3, comparator_12_eq, and_31_out);
  Comparator #(.width(2), .mode("unsigned")) comparator_12 (
    .a(index), .b(2'b11), .eq(comparator_12_eq));  // open: gt, lt

  // Other names for the same wires on the sheet: m[1:0] = UpdatePC[1:0]; tag[29:0] = UpdatePC[31:2]
endmodule

module InputGen (
  input  Clock,
  output [31:0] PredPC,
  output [31:0] UpdatePC,
  output IsBranch,
  output BranchTaken,
  output [31:0] BranchDestAddress
);

  wire [7:0] counter_1_q;

  Counter #(.max('h1b), .ongoal("stay")) counter_1 (
    .count(1'b1), .Q(counter_1_q), .clk(Clock));  // open: load, D, carry, clr
  ROM #(.dataWidth(32)) rom_1 (.addr(counter_1_q), .data(PredPC));  // open: sel
  ROM #(.dataWidth(1)) rom_2 (.addr(counter_1_q), .data(IsBranch));  // open: sel
  ROM #(.dataWidth(1)) rom_3 (.addr(counter_1_q), .data(BranchTaken));  // open: sel
  ROM #(.dataWidth(32)) rom_4 (.addr(counter_1_q), .data(BranchDestAddress));  // open: sel

  assign UpdatePC = PredPC;

  // Notes on the sheet:
  //   Counter max count is 27 because there are only 28 instructions
  //   contents of rom_1 (hex, n*v repeats v):
  //   5*0 1 1 1 5 2 2 2 3 3 3 0 0 4
  //   contents of rom_2 (hex, n*v repeats v):
  //   8*1 0 8*1 0 10*1
  //   contents of rom_3 (hex, n*v repeats v):
  //   8*1 0 6*1 4*0 1 0 1 0 1 0 1 0 1
  //   contents of rom_4 (hex, n*v repeats v):
  //   5*60 5f 5f 5f 0 5 5 5 8 8 8 60 60 0 10*60
endmodule

module Test (
  input  TakeBranch,
  input  [31:0] PredBranchAddress,
  input  Clock,
  output IsPredCorrect,
  output CorrectPred,
  output IsPredBranchCorrect,
  output [31:0] CorrectPredBranch,
  output Correct,
  output Done
);

  wire comparator_1_eq, comparator_2_eq, DontCare, not_1_out;
  wire [7:0] Count;

  Counter #(.max('h1c), .ongoal("stay")) counter_1 (.count(1'b1), .Q(Count), .clk(Clock));  // open: load, D, carry, clr
  ROM #(.dataWidth(1)) rom_1 (.addr(Count), .data(CorrectPred));  // open: sel
  ROM #(.dataWidth(32)) rom_2 (.addr(Count), .data(CorrectPredBranch));  // open: sel
  ROM #(.dataWidth(1)) rom_3 (.addr(Count), .data(DontCare));  // open: sel
  not not_1 (not_1_out, CorrectPred);
  Comparator #(.width(1), .mode("unsigned")) comparator_1 (
    .a(TakeBranch), .b(CorrectPred), .eq(comparator_1_eq));  // open: gt, lt
  or or_1 (IsPredCorrect, comparator_1_eq, DontCare);
  Comparator #(.width(32), .mode("unsigned")) comparator_2 (
    .a(PredBranchAddress), .b(CorrectPredBranch), .eq(comparator_2_eq));  // open: gt, lt
  Comparator #(.mode("unsigned")) comparator_3 (.a(Count), .b(8'h1c), .eq(Done));  // open: gt, lt
  // Probe on Count
  or or_2 (IsPredBranchCorrect, comparator_2_eq, not_1_out, DontCare);
  and and_1 (Correct, IsPredCorrect, IsPredBranchCorrect);

  // Notes on the sheet:
  //   Correct Take Branch
  //   Correct Prediction Branch Address
  //   Don't Care
  //   contents of rom_1 (hex, n*v repeats v):
  //   4*0 1 0 0 1 0 0 0 1 0 0 1 1 9*0 1 0 1
  //   contents of rom_2 (hex, n*v repeats v):
  //   0 0 0 60 60 0 5f 5f 5f 60 5 5 60 8 8 60 5f 8 8 60 5 7*60
  //   contents of rom_3 (hex, n*v repeats v):
  //   8*0 1 8*0 1
endmodule

module Gshare_1 (
  input  [31:0] _1_or_0
);

  wire and_3_out, Clock, comparator_1_eq, comparator_2_eq;
  wire [31:0] address, and_1_out, and_2_out, and_4_out, branchTaken, historyBuffer, mask, or_1_out, PC,
       shifter_1_out, Tag_q;

  Register #(.width(32)) u_PC (.Q(PC));  // open: D, en, clk, clr
  Register #(.width(32)) u_historyBuffer (.D(or_1_out), .Q(historyBuffer));  // open: en, clk, clr
  assign and_1_out = PC & mask;  // AND_Gate and_1, 32 bits wide
  assign and_2_out = historyBuffer & mask;  // AND_Gate and_2, 32 bits wide
  Register #(.width(32)) Tag (.Q(Tag_q));  // open: D, en, clk, clr
  Clock clock_1 (.out(Clock));
  Comparator #(.width(32), .mode("unsigned")) comparator_1 (.a(Tag_q), .b(PC), .eq(comparator_1_eq));  // open: gt, lt
  Comparator #(.width(32), .mode("unsigned")) comparator_2 (
    .a(branchTaken), .b(_1_or_0), .eq(comparator_2_eq));  // open: gt, lt
  assign address = and_1_out ^ and_2_out;  // XOR_Gate xor_1, 32 bits wide
  and and_3 (and_3_out, comparator_1_eq, comparator_2_eq);
  Shifter #(.width(32)) shifter_1 (.in(historyBuffer), .\dist (5'b00001), .out(shifter_1_out));
  assign and_4_out = shifter_1_out & mask;  // AND_Gate and_4, 32 bits wide
  assign or_1_out = and_4_out | branchTaken;  // OR_Gate or_1, 32 bits wide

  // Notes on the sheet:
  //   address = (PC & self.mask) ^ (self.historyBuffer & self.mask)
  //   self.historyBuffer = ((self.historyBuffer << 1) & self.mask) | int(branchTaken)
  //   output = count up branch taken, count down branch taken, set 1, or set 0
endmodule
