// Logisim project MultiCycleMips-ExcludesJal.circ as structural Verilog: 10 circuits, main circuit 32bit +/-
// 1
module Main (
  input  in_1,
  input  in_2,
  input  in_3,
  output [4:0] out_4,
  output [1:0] out_5,
  output [7:0] out_6,
  output [7:0] out_7,
  output [5:0] out_8,
  output [5:0] out_9,
  output [31:0] out_10,
  output [31:0] out_11
);

  wire ALUSrcA, and_1_out, Clock, comparator_1_eq, comparator_2_eq, control_1_pcwrite, control_1_pcwritecond,
       IorD, IRWrite, MemRead, MemtoReg, MemWrite, not_1_out, or_1_out, or_2_out, RegDst, RegWrite, Zero;
  wire [1:0] ALUOp, PCSource;
  wire [2:0] alucontrol2_1_oper0, multiplexer_6_out;
  wire [4:0] multiplexer_2_out;
  wire [6:0] bit_extender_1_out;
  wire [7:0] multiplexer_1_out;
  wire [25:6] IR_q;
  wire [31:0] A_q, alu_1_aluresult, ALUOut_q, bit_extender_3_out, bit_extender_4_out, MDR_q,
       multiplexer_3_out, multiplexer_4_out, multiplexer_7_out, PC_q, ram_1_data, regfile_1_rddata1,
       shifter_1_out, shifter_2_out, WriteData;

  or or_1 (or_1_out, and_1_out, control_1_pcwrite);
  and and_1 (and_1_out, Zero, control_1_pcwritecond);
  Register #(.width(32)) PC (.D(multiplexer_7_out), .en(or_1_out), .Q(PC_q), .clk(Clock));  // open: clr
  Control control_1 (
    .Op5(out_8[0]), .Op4(out_8[1]), .Op3(out_8[2]), .Op2(out_8[3]), .Op1(out_8[4]), .Op0(out_8[5]),
    .Clock(Clock), .PCWrite(control_1_pcwrite), .PCWriteCond(control_1_pcwritecond), .IorD(IorD),
    .MemRead(MemRead), .MemWrite(MemWrite), .IRWrite(IRWrite), .MemtoReg(MemtoReg), .PCSource(PCSource),
    .ALUOp(ALUOp), .ALUSrcB(out_5), .ALUSrcA(ALUSrcA), .RegWrite(RegWrite), .RegDst(RegDst));  // open: out_8, out_10, out_11
  Bit_Extender #(.in_width(30), .out_width(7)) bit_extender_1 (.in(PC_q[31:2]), .out(bit_extender_1_out));
  Bit_Extender #(.in_width(32), .out_width(7)) bit_extender_2 (.in(ALUOut_q), .out(out_7[6:0]));
  Multiplexer #(.width(8), .enable("false")) multiplexer_1 (
    .in0({1'b0, bit_extender_1_out}), .in1({1'b1, out_7[6:0]}), .out(multiplexer_1_out), .sel(IorD));
  not not_1 (not_1_out, MemWrite);
  RAM #(.dataWidth(32)) ram_1 (
    .addr(multiplexer_1_out), .data(ram_1_data), .clk(Clock), .ld(not_1_out));  // open: sel, clr
  assign ram_1_data = MemWrite ? WriteData : 32'bz;  // Controlled_Buffer controlled_buffer_1
  Register #(.width(32)) MDR (.D(ram_1_data), .Q(MDR_q), .clk(Clock));  // open: en, clr
  Register #(.width(32)) IR (.D(ram_1_data), .en(IRWrite), .Q({out_8, IR_q, out_9}), .clk(Clock));  // open: clr
  Multiplexer #(.width(5), .enable("false")) multiplexer_2 (
    .in0(IR_q[20:16]), .in1(IR_q[15:11]), .out(multiplexer_2_out), .sel(RegDst));
  Multiplexer #(.width(32), .enable("false")) multiplexer_3 (
    .in0(ALUOut_q), .in1(MDR_q), .out(multiplexer_3_out), .sel(MemtoReg));
  RegFile regfile_1 (
    .WrAddr(multiplexer_2_out), .WrData(multiplexer_3_out), .WrReg(RegWrite), .RdAddr1(IR_q[25:21]),
    .RdAddr2(IR_q[20:16]), .RdData1(regfile_1_rddata1), .RdData2(out_11), .Clock(Clock));
  Register #(.width(32)) A (.D(regfile_1_rddata1), .Q(A_q), .clk(Clock));  // open: en, clr
  Register #(.width(32)) B (.D(out_11), .Q(WriteData), .clk(Clock));  // open: en, clr
  assign bit_extender_3_out = {{16{1'b0}}, {IR_q[15:6], out_9}};  // Bit_Extender bit_extender_3
  Clock clock_1 (.out(Clock));
  Multiplexer #(.width(32), .enable("false")) multiplexer_4 (
    .in0(PC_q), .in1(A_q), .out(multiplexer_4_out), .sel(ALUSrcA));
  Multiplexer #(.select(2), .width(32), .enable("false")) multiplexer_5 (
    .in0(WriteData), .in1(32'h4), .in2(bit_extender_3_out), .in3(shifter_1_out), .out(out_10), .sel(out_5));
  Shifter #(.width(32)) shifter_1 (.in(bit_extender_3_out), .\dist (5'b00010), .out(shifter_1_out));
  Multiplexer #(.width(3), .enable("false")) multiplexer_6 (
    .in0(alucontrol2_1_oper0), .in1(3'b010), .out(multiplexer_6_out), .sel(or_2_out));
  ALU alu_1 (
    .ALUCtl(multiplexer_6_out), .A(multiplexer_4_out), .B(out_10), .ALUResult(alu_1_aluresult), .Zero(Zero),
    .Shamt(IR_q[10:6]));  // open: Overflow
  // Probe on nothing
  // Probe on nothing
  // Probe on nothing
  // Probe on nothing
  // Probe on nothing
  // Probe on nothing
  // Probe on nothing
  assign bit_extender_4_out = {{6{1'b0}}, {IR_q, out_9}};  // Bit_Extender bit_extender_4
  ALUControl2 alucontrol2_1 (
    .ALU1(ALUOp[0]), .ALU0(ALUOp[1]), .F5(out_9[5]), .F4(out_9[4]), .F3(out_9[3]), .F2(out_9[2]),
    .F1(out_9[1]), .F0(out_9[0]), .Oper2(alucontrol2_1_oper0[2]), .Oper1(alucontrol2_1_oper0[1]),
    .Oper0(alucontrol2_1_oper0[0]));
  Register #(.width(32)) ALUOut (.D(alu_1_aluresult), .Q(ALUOut_q), .clk(Clock));  // open: en, clr
  Shifter #(.width(32)) shifter_2 (.in(bit_extender_4_out), .\dist (5'b00010), .out(shifter_2_out));
  or or_2 (or_2_out, comparator_1_eq, comparator_2_eq);
  Multiplexer #(.select(2), .width(32), .enable("false")) multiplexer_7 (
    .in0(alu_1_aluresult), .in1(ALUOut_q), .in2(shifter_2_out), .out(multiplexer_7_out), .sel(PCSource));  // open: in3
  Comparator #(.width(2), .mode("unsigned")) comparator_1 (.a(2'b11), .b(out_5), .eq(comparator_1_eq));  // open: gt, lt
  Comparator #(.width(2), .mode("unsigned")) comparator_2 (.a(2'b01), .b(out_5), .eq(comparator_2_eq));  // open: gt, lt

  assign out_7[7] = 1'b1;

  // Other names for the same wires on the sheet: Function[5:0] = out_9; Opcode[5:0] = out_8; ALUSrcB[1:0] = out_5

  // Notes on the sheet:
  //   shamt
  //   To PC
  //   To RAM Addr.
endmodule

module _32bit (
  input  Add_Sub_control,
  input  [31:0] in_2,
  input  [31:0] in_3,
  output [31:0] out_4,
  output carry_out
);

  wire adder_1_cout, subtractor_1_bout;
  wire [31:0] adder_1_out, subtractor_1_out;

  Adder #(.width(32)) adder_1 (.a(in_2), .b(in_3), .out(adder_1_out), .cout(adder_1_cout));  // open: cin
  Subtractor #(.width(32)) subtractor_1 (
    .a(in_2), .b(in_3), .out(subtractor_1_out), .bout(subtractor_1_bout));  // open: bin
  Multiplexer #(.width(32), .enable("false")) multiplexer_1 (
    .in0(adder_1_out), .in1(subtractor_1_out), .out(out_4), .sel(Add_Sub_control));
  Multiplexer #(.enable("false")) multiplexer_2 (
    .in0(adder_1_cout), .in1(subtractor_1_bout), .out(carry_out), .sel(Add_Sub_control));
endmodule

module ALU (
  input  [2:0] ALUCtl,
  input  [31:0] A,
  input  [31:0] B,
  input  [4:0] Shamt,
  output [31:0] ALUResult,
  output Zero,
  output Overflow
);

  wire and_2_out, and_3_out, comparator_1_lt, not_1_out, not_2_out, not_3_out, not_4_out, not_5_out, or_2_out;
  wire [31:0] Add, And, LessThan, Nor, Or, ShiftLeft, ShiftRight, Sub, Xor;

  Adder #(.width(32)) adder_1 (.a(A), .b(B), .out(Add));  // open: cin, cout
  Subtractor #(.width(32)) subtractor_1 (.a(A), .b(B), .out(Sub));  // open: bin, bout
  assign And = A & B;  // AND_Gate and_1, 32 bits wide
  assign Or = A | B;  // OR_Gate or_1, 32 bits wide
  assign Nor = ~(A | B);  // NOR_Gate nor_1, 32 bits wide
  Comparator #(.width(32)) comparator_1 (.a(A), .b(B), .lt(comparator_1_lt));  // open: gt, eq
  assign LessThan = {{31{1'b0}}, comparator_1_lt};  // Bit_Extender bit_extender_1
  Shifter #(.width(32)) shifter_1 (.in(B), .\dist (Shamt), .out(ShiftLeft));
  Shifter #(.width(32), .shift("lr")) shifter_2 (.in(B), .\dist (Shamt), .out(ShiftRight));
  not not_1 (not_1_out, ALUCtl[0]);
  not not_2 (not_2_out, ALUCtl[1]);
  not not_3 (not_3_out, ALUCtl[2]);
  not not_4 (not_4_out, ALUCtl[0]);
  not not_5 (not_5_out, ALUCtl[2]);
  and and_2 (and_2_out, not_1_out, not_2_out, not_3_out);
  and and_3 (and_3_out, not_4_out, ALUCtl[1], not_5_out);
  Multiplexer #(.select(3), .width(32), .enable("false")) multiplexer_1 (
    .in0(Sub), .in1(And), .in2(Add), .in3(Or), .in4(LessThan), .in5(ShiftLeft), .in6(ShiftRight), .in7(Xor),
    .out(ALUResult), .sel(ALUCtl));
  Overflow overflow_1 (
    .Add(and_3_out), .Sub(and_2_out), .ASign(A[31]), .BSign(B[31]), .ResultSign(ALUResult[31]),
    .Overflow(Overflow));
  or or_2 (or_2_out, ALUResult[0], ALUResult[1], ALUResult[2], ALUResult[3], ALUResult[4], ALUResult[5], ALUResult[6], ALUResult[7], ALUResult[8], ALUResult[9], ALUResult[10], ALUResult[11], ALUResult[12], ALUResult[13], ALUResult[14], ALUResult[15], ALUResult[16], ALUResult[17], ALUResult[18], ALUResult[19], ALUResult[20], ALUResult[21], ALUResult[22], ALUResult[23], ALUResult[24], ALUResult[25], ALUResult[26], ALUResult[27], ALUResult[28], ALUResult[29], ALUResult[30], ALUResult[31]);
  not not_6 (Zero, or_2_out);

  // Other names for the same wires on the sheet: ASign = A[31]; ResultSign = ALUResult[31]; BSign = B[31]
endmodule

module RegFile (
  input  [4:0] WrAddr,
  input  [31:0] WrData,
  input  WrReg,
  input  [4:0] RdAddr1,
  input  [4:0] RdAddr2,
  input  Clock,
  output [31:0] RdData1,
  output [31:0] RdData2
);

  wire WrReg0, WrReg1, WrReg2, WrReg3, WrReg4, WrReg5, WrReg6, WrReg7, WrReg8, WrReg9, WrReg10, WrReg11,
       WrReg12, WrReg13, WrReg14, WrReg15, WrReg16, WrReg17, WrReg18, WrReg19, WrReg20, WrReg21, WrReg22,
       WrReg23, WrReg24, WrReg25, WrReg26, WrReg27, WrReg28, WrReg29, WrReg30, WrReg31;
  wire [31:0] RegData1, RegData2, RegData3, RegData4, RegData5, RegData6, RegData7, RegData8, RegData9,
       RegData10, RegData11, RegData12, RegData13, RegData14, RegData15, RegData16, RegData17, RegData18,
       RegData19, RegData20, RegData21, RegData22, RegData23, RegData24, RegData25, RegData26, RegData27,
       RegData28, RegData29, RegData30, RegData31;

  Demultiplexer #(.select(5), .enable("false")) demultiplexer_1 (
    .out0(WrReg0), .out1(WrReg1), .out2(WrReg2), .out3(WrReg3), .out4(WrReg4), .out5(WrReg5), .out6(WrReg6),
    .out7(WrReg7), .out8(WrReg8), .out9(WrReg9), .out10(WrReg10), .out11(WrReg11), .out12(WrReg12),
    .out13(WrReg13), .out14(WrReg14), .out15(WrReg15), .out16(WrReg16), .out17(WrReg17), .out18(WrReg18),
    .out19(WrReg19), .out20(WrReg20), .out21(WrReg21), .out22(WrReg22), .out23(WrReg23), .out24(WrReg24),
    .out25(WrReg25), .out26(WrReg26), .out27(WrReg27), .out28(WrReg28), .out29(WrReg29), .out30(WrReg30),
    .out31(WrReg31), .in(WrReg), .sel(WrAddr));
  Register #(.width(32)) Reg4 (.D(WrData), .en(WrReg4), .Q(RegData4), .clk(Clock));  // open: clr
  Register #(.width(32)) Reg8 (.D(WrData), .en(WrReg8), .Q(RegData8), .clk(Clock));  // open: clr
  Register #(.width(32)) Reg12 (.D(WrData), .en(WrReg12), .Q(RegData12), .clk(Clock));  // open: clr
  Register #(.width(32)) Reg16 (.D(WrData), .en(WrReg16), .Q(RegData16), .clk(Clock));  // open: clr
  Register #(.width(32)) Reg20 (.D(WrData), .en(WrReg20), .Q(RegData20), .clk(Clock));  // open: clr
  Register #(.width(32)) Reg24 (.D(WrData), .en(WrReg24), .Q(RegData24), .clk(Clock));  // open: clr
  Register #(.width(32)) Reg28 (.D(WrData), .en(WrReg28), .Q(RegData28), .clk(Clock));  // open: clr
  Register #(.width(32)) Reg1 (.D(WrData), .en(WrReg1), .Q(RegData1), .clk(Clock));  // open: clr
  Register #(.width(32)) Reg5 (.D(WrData), .en(WrReg5), .Q(RegData5), .clk(Clock));  // open: clr
  Register #(.width(32)) Reg9 (.D(WrData), .en(WrReg9), .Q(RegData9), .clk(Clock));  // open: clr
  Register #(.width(32)) Reg13 (.D(WrData), .en(WrReg13), .Q(RegData13), .clk(Clock));  // open: clr
  Register #(.width(32)) Reg17 (.D(WrData), .en(WrReg17), .Q(RegData17), .clk(Clock));  // open: clr
  Register #(.width(32)) Reg21 (.D(WrData), .en(WrReg21), .Q(RegData21), .clk(Clock));  // open: clr
  Register #(.width(32)) Reg25 (.D(WrData), .en(WrReg25), .Q(RegData25), .clk(Clock));  // open: clr
  Register #(.width(32)) Reg29 (.D(WrData), .en(WrReg29), .Q(RegData29), .clk(Clock));  // open: clr
  Register #(.width(32)) Reg2 (.D(WrData), .en(WrReg2), .Q(RegData2), .clk(Clock));  // open: clr
  Register #(.width(32)) Reg6 (.D(WrData), .en(WrReg6), .Q(RegData6), .clk(Clock));  // open: clr
  Register #(.width(32)) Reg10 (.D(WrData), .en(WrReg10), .Q(RegData10), .clk(Clock));  // open: clr
  Register #(.width(32)) Reg14 (.D(WrData), .en(WrReg14), .Q(RegData14), .clk(Clock));  // open: clr
  Register #(.width(32)) Reg18 (.D(WrData), .en(WrReg18), .Q(RegData18), .clk(Clock));  // open: clr
  Register #(.width(32)) Reg22 (.D(WrData), .en(WrReg22), .Q(RegData22), .clk(Clock));  // open: clr
  Register #(.width(32)) Reg26 (.D(WrData), .en(WrReg26), .Q(RegData26), .clk(Clock));  // open: clr
  Register #(.width(32)) Reg30 (.D(WrData), .en(WrReg30), .Q(RegData30), .clk(Clock));  // open: clr
  Register #(.width(32)) Reg3 (.D(WrData), .en(WrReg3), .Q(RegData3), .clk(Clock));  // open: clr
  Register #(.width(32)) Reg7 (.D(WrData), .en(WrReg7), .Q(RegData7), .clk(Clock));  // open: clr
  Register #(.width(32)) Reg11 (.D(WrData), .en(WrReg11), .Q(RegData11), .clk(Clock));  // open: clr
  Register #(.width(32)) Reg15 (.D(WrData), .en(WrReg15), .Q(RegData15), .clk(Clock));  // open: clr
  Register #(.width(32)) Reg19 (.D(WrData), .en(WrReg19), .Q(RegData19), .clk(Clock));  // open: clr
  Register #(.width(32)) Reg23 (.D(WrData), .en(WrReg23), .Q(RegData23), .clk(Clock));  // open: clr
  Register #(.width(32)) Reg27 (.D(WrData), .en(WrReg27), .Q(RegData27), .clk(Clock));  // open: clr
  Register #(.width(32)) Reg31 (.D(WrData), .en(WrReg31), .Q(RegData31), .clk(Clock));  // open: clr
  Multiplexer #(.select(5), .width(32), .enable("false")) multiplexer_1 (
    .in0({32{1'b0}}), .in1(RegData1), .in2(RegData2), .in3(RegData3), .in4(RegData4), .in5(RegData5),
    .in6(RegData6), .in7(RegData7), .in8(RegData8), .in9(RegData9), .in10(RegData10), .in11(RegData11),
    .in12(RegData12), .in13(RegData13), .in14(RegData14), .in15(RegData15), .in16(RegData16),
    .in17(RegData17), .in18(RegData18), .in19(RegData19), .in20(RegData20), .in21(RegData21),
    .in22(RegData22), .in23(RegData23), .in24(RegData24), .in25(RegData25), .in26(RegData26),
    .in27(RegData27), .in28(RegData28), .in29(RegData29), .in30(RegData30), .in31(RegData31), .out(RdData1),
    .sel(RdAddr1));
  Multiplexer #(.select(5), .width(32), .enable("false")) multiplexer_2 (
    .in0({32{1'b0}}), .in1(RegData1), .in2(RegData2), .in3(RegData3), .in4(RegData4), .in5(RegData5),
    .in6(RegData6), .in7(RegData7), .in8(RegData8), .in9(RegData9), .in10(RegData10), .in11(RegData11),
    .in12(RegData12), .in13(RegData13), .in14(RegData14), .in15(RegData15), .in16(RegData16),
    .in17(RegData17), .in18(RegData18), .in19(RegData19), .in20(RegData20), .in21(RegData21),
    .in22(RegData22), .in23(RegData23), .in24(RegData24), .in25(RegData25), .in26(RegData26),
    .in27(RegData27), .in28(RegData28), .in29(RegData29), .in30(RegData30), .in31(RegData31), .out(RdData2),
    .sel(RdAddr2));
endmodule

module Overflow (
  input  Add,
  input  Sub,
  input  ASign,
  input  BSign,
  input  ResultSign,
  output Overflow
);

  wire and_1_out, and_2_out, or_1_out, xnor_1_out, xor_1_out, xor_2_out;

  xnor xnor_1 (xnor_1_out, ASign, BSign);
  xor xor_1 (xor_1_out, ASign, BSign);
  and and_1 (and_1_out, xnor_1_out, Add);
  and and_2 (and_2_out, xor_1_out, Sub);
  or or_1 (or_1_out, and_1_out, and_2_out);
  xor xor_2 (xor_2_out, ResultSign, ASign);
  and and_3 (Overflow, or_1_out, xor_2_out);

  // Notes on the sheet:
  //   Overflow occurs when doing addition and sign(A) == sign(B) && sign(result) != sign(A)
  //   Or
  //   Overflow occurs when doing subtraction and sign(A) != sign(B) && sign(result) != sign(A)
endmodule

module OpcodeDecode (
  input  Op5,
  input  Op4,
  input  Op3,
  input  Op2,
  input  Op1,
  input  Op0,
  output R,
  output lw,
  output sw,
  output J,
  output beq
);

  wire and_1_out, and_2_out, and_6_out, and_7_out, not_1_out, not_2_out, not_3_out, not_4_out, not_5_out,
       not_6_out, not_7_out, not_8_out, not_9_out, not_10_out, not_11_out, not_12_out, not_13_out,
       not_14_out, not_15_out, not_16_out, not_17_out, not_18_out, not_19_out, not_20_out, not_21_out,
       not_22_out, not_23_out, not_24_out, not_25_out, not_26_out;

  not not_1 (not_1_out, Op5);
  not not_2 (not_2_out, Op3);
  not not_3 (not_3_out, Op2);
  not not_4 (not_4_out, Op1);
  not not_5 (not_5_out, Op0);
  not not_6 (not_6_out, Op4);
  not not_7 (not_7_out, Op3);
  not not_8 (not_8_out, Op2);
  not not_9 (not_9_out, Op0);
  not not_10 (not_10_out, Op4);
  not not_11 (not_11_out, Op3);
  not not_12 (not_12_out, Op2);
  not not_13 (not_13_out, Op4);
  not not_14 (not_14_out, Op2);
  not not_15 (not_15_out, Op5);
  not not_16 (not_16_out, Op4);
  not not_17 (not_17_out, Op3);
  not not_18 (not_18_out, Op2);
  not not_19 (not_19_out, Op0);
  not not_20 (not_20_out, Op5);
  not not_21 (not_21_out, Op4);
  not not_22 (not_22_out, Op3);
  not not_23 (not_23_out, Op1);
  not not_24 (not_24_out, Op0);
  not not_25 (not_25_out, Op5);
  not not_26 (not_26_out, Op4);
  and and_1 (and_1_out, not_1_out, Op4, not_2_out, not_3_out, not_4_out, not_5_out);
  and and_2 (and_2_out, Op5, not_6_out, not_7_out, not_8_out, not_9_out);
  and and_3 (lw, Op5, not_10_out, not_11_out, not_12_out, Op1, Op0);
  and and_4 (sw, Op5, not_13_out, Op3, not_14_out, Op1, Op0);
  and and_5 (J, not_15_out, not_16_out, not_17_out, not_18_out, Op1, not_19_out);
  and and_6 (and_6_out, not_20_out, not_21_out, not_22_out, Op2, not_23_out, not_24_out);
  and and_7 (and_7_out, not_25_out, not_26_out, Op3, Op2, Op1, Op0);
  or or_1 (R, and_1_out, and_2_out);
  or or_2 (beq, and_6_out, and_7_out);
endmodule

module Control (
  input  Op5,
  input  Op4,
  input  Op3,
  input  Op2,
  input  Op1,
  input  Op0,
  input  Clock,
  output [9:0] out_8,
  output PCWrite,
  output [3:0] out_10,
  output [15:0] out_11,
  output PCWriteCond,
  output IorD,
  output MemRead,
  output MemWrite,
  output IRWrite,
  output MemtoReg,
  output [1:0] PCSource,
  output [1:0] ALUOp,
  output [1:0] ALUSrcB,
  output ALUSrcA,
  output RegWrite,
  output RegDst
);

  ROM #(.addrWidth(10), .dataWidth(4)) rom_1 (
    .addr({Op5, Op4, Op3, Op2, Op1, Op0, out_8[3:0]}), .data(out_10));  // open: sel
  Register #(.width(4)) register_1 (.D(out_10), .Q(out_8[3:0]), .clk(Clock));  // open: en, clr
  ROM #(.addrWidth(4), .dataWidth(16)) rom_2 (
    .addr(out_8[3:0]),
    .data({out_11[15:14], IorD, MemRead, MemWrite, IRWrite, MemtoReg, out_11[8:7], ALUOp[0], ALUOp[1], ALUSrcB, ALUSrcA, out_11[1:0]}));  // open: sel

  assign out_8[9:4] = {Op5, Op4, Op3, Op2, Op1, Op0};
  assign {out_11[13:9], out_11[6:2]} = {IorD, MemRead, MemWrite, IRWrite, MemtoReg, ALUOp[0], ALUOp[1], ALUSrcB, ALUSrcA};
  assign PCSource = out_11[8:7];
  assign PCWrite = out_11[15];
  assign PCWriteCond = out_11[14];
  assign RegDst = out_11[0];
  assign RegWrite = out_11[1];

  // Notes on the sheet:
  //   contents of rom_1 (hex, n*v repeats v):
  //   1 6 4*0 7 57*0 1 a 4*0 b 0 0 0 b 53*0 1 8 62*0 1 a 8*0 b 117*0 1 a 8*0 b 61*0 7 119*0 1 6 4*0 7 0 6
  //   183*0 1 a 8*0 b 53*0 1 9 14*0 1 2 3 4 60*0 1 2 5
  //   contents of rom_2 (hex, n*v repeats v):
  //   9408 18 14 3000 202 2800 44 3 40a4 8100 14 82 3
endmodule

module Extra (
  input  in_1,
  input  in_2,
  input  in_3,
  input  in_4,
  input  in_5,
  input  in_6
);

  wire [4:0] opcodedecode_1_r;

  OpcodeDecode opcodedecode_1 (
    .Op5(in_1), .Op4(in_2), .Op3(in_3), .Op2(in_4), .Op1(in_5), .Op0(in_6), .R(opcodedecode_1_r[0]),
    .lw(opcodedecode_1_r[1]), .sw(opcodedecode_1_r[2]), .J(opcodedecode_1_r[3]), .beq(opcodedecode_1_r[4]));

  // Other names for the same wires on the sheet: Opcode[5:0] = {in_6, in_5, in_4, in_3, in_2, in_1}
endmodule

module ALUControl8 (
  input  ALU1,
  input  ALU0,
  input  F3,
  input  F2,
  input  F1,
  input  F0,
  output Oper2,
  output Oper1,
  output Oper0
);

  wire and_1_out, and_2_out, and_3_out, and_4_out, and_5_out, and_6_out, and_7_out, and_8_out, and_9_out,
       and_10_out, and_11_out, and_12_out, and_13_out, and_14_out, and_15_out, and_16_out, and_17_out,
       and_18_out, and_19_out, and_20_out, and_21_out, not_1_out, not_2_out, not_3_out, not_4_out, not_5_out,
       not_6_out, not_7_out, not_8_out, not_9_out, not_10_out, not_11_out, not_12_out, not_13_out,
       not_14_out, not_15_out, not_16_out, not_17_out, not_18_out, not_19_out, not_20_out, not_21_out,
       not_22_out, not_23_out, not_24_out, not_25_out, not_26_out, not_27_out, not_28_out, not_29_out,
       not_30_out, not_31_out, not_32_out, not_33_out, not_34_out, not_35_out, not_36_out, not_37_out,
       not_38_out, not_39_out, not_40_out, not_41_out, not_42_out, not_43_out, not_44_out, not_45_out,
       not_46_out;

  not not_1 (not_1_out, ALU1);
  not not_2 (not_2_out, ALU0);
  not not_3 (not_3_out, F3);
  not not_4 (not_4_out, F2);
  not not_5 (not_5_out, F1);
  not not_6 (not_6_out, F0);
  not not_7 (not_7_out, ALU0);
  not not_8 (not_8_out, F2);
  not not_9 (not_9_out, F0);
  not not_10 (not_10_out, ALU1);
  not not_11 (not_11_out, F3);
  not not_12 (not_12_out, F1);
  not not_13 (not_13_out, ALU0);
  not not_14 (not_14_out, F2);
  not not_15 (not_15_out, F1);
  not not_16 (not_16_out, F0);
  not not_17 (not_17_out, ALU0);
  not not_18 (not_18_out, F2);
  not not_19 (not_19_out, ALU0);
  not not_20 (not_20_out, F1);
  not not_21 (not_21_out, ALU1);
  not not_22 (not_22_out, ALU0);
  not not_23 (not_23_out, F3);
  not not_24 (not_24_out, ALU1);
  not not_25 (not_25_out, ALU0);
  not not_26 (not_26_out, F0);
  not not_27 (not_27_out, ALU1);
  not not_28 (not_28_out, ALU0);
  not not_29 (not_29_out, F1);
  not not_30 (not_30_out, F2);
  not not_31 (not_31_out, F1);
  not not_32 (not_32_out, ALU0);
  not not_33 (not_33_out, F3);
  not not_34 (not_34_out, F2);
  not not_35 (not_35_out, F1);
  not not_36 (not_36_out, ALU1);
  not not_37 (not_37_out, ALU0);
  not not_38 (not_38_out, F3);
  not not_39 (not_39_out, F2);
  not not_40 (not_40_out, F1);
  not not_41 (not_41_out, F0);
  not not_42 (not_42_out, ALU1);
  not not_43 (not_43_out, ALU0);
  not not_44 (not_44_out, F3);
  not not_45 (not_45_out, F2);
  not not_46 (not_46_out, ALU0);
  and and_1 (and_1_out, not_1_out, not_2_out, not_3_out, not_4_out, not_5_out, not_6_out);
  and and_2 (and_2_out, not_7_out, F3, not_8_out, F1, not_9_out);
  and and_3 (and_3_out, not_10_out, ALU0, not_11_out, F2, not_12_out, F0);
  and and_4 (and_4_out, ALU1, not_13_out, F3);
  and and_5 (and_5_out, ALU1, F3, not_14_out);
  and and_6 (and_6_out, ALU1, F3, not_15_out);
  and and_7 (and_7_out, ALU1, F3, not_16_out);
  and and_8 (and_8_out, not_17_out, not_18_out, F0);
  and and_9 (and_9_out, not_19_out, not_20_out, F0);
  and and_10 (and_10_out, not_21_out, not_22_out, not_23_out, F1);
  and and_11 (and_11_out, not_24_out, not_25_out, F2, not_26_out);
  and and_12 (and_12_out, not_27_out, not_28_out, F3, not_29_out);
  and and_13 (and_13_out, ALU1, not_30_out, not_31_out);
  and and_14 (and_14_out, ALU1, not_32_out, F0);
  and and_15 (and_15_out, ALU1, not_33_out, F0);
  and and_16 (and_16_out, ALU1, not_34_out, F0);
  and and_17 (and_17_out, ALU1, not_35_out, F0);
  and and_18 (and_18_out, not_36_out, not_37_out, not_38_out, not_39_out, not_40_out, not_41_out);
  and and_19 (and_19_out, not_42_out, not_43_out, not_44_out, not_45_out, F1, F0);
  and and_20 (and_20_out, not_46_out, F3, F2, F1, F0);
  and and_21 (and_21_out, ALU1, F2);
  or or_1 (Oper2, and_1_out, and_2_out, and_3_out, and_4_out, and_5_out, and_6_out, and_7_out);
  or or_2 (Oper1, and_8_out, and_9_out, and_10_out, and_11_out, and_12_out, and_13_out, and_14_out, and_15_out, and_16_out, and_17_out);
  or or_3 (Oper0, and_18_out, and_19_out, and_20_out, and_21_out);
endmodule

module ALUControl2 (
  input  ALU1,
  input  ALU0,
  input  F5,
  input  F4,
  input  F3,
  input  F2,
  input  F1,
  input  F0,
  output Oper2,
  output Oper1,
  output Oper0
);

  wire and_1_out, and_2_out, and_3_out, and_4_out, and_5_out, and_6_out, and_7_out, and_8_out, and_9_out,
       and_10_out, and_11_out, and_12_out, and_13_out, and_14_out, and_15_out, and_16_out, and_17_out,
       and_18_out, and_19_out, and_20_out, and_21_out, and_22_out, and_23_out, and_24_out, and_25_out,
       and_26_out, and_27_out, and_28_out, and_29_out, and_30_out, and_31_out, and_32_out, not_1_out,
       not_2_out, not_3_out, not_4_out, not_5_out, not_6_out, not_7_out, not_8_out, not_9_out, not_10_out,
       not_11_out, not_12_out, not_13_out, not_14_out, not_15_out, not_16_out, not_17_out, not_18_out,
       not_19_out, not_20_out, not_21_out, not_22_out, not_23_out, not_24_out, not_25_out, not_26_out,
       not_27_out, not_28_out, not_29_out, not_30_out, not_31_out, not_32_out, not_33_out, not_34_out,
       not_35_out, not_36_out, not_37_out, not_38_out, not_39_out, not_40_out, not_41_out, not_42_out,
       not_43_out, not_44_out, not_45_out, not_46_out, not_47_out, not_48_out, not_49_out, not_50_out,
       not_51_out, not_52_out, not_53_out, not_54_out, not_55_out, not_56_out, not_57_out, not_58_out,
       not_59_out, not_60_out, not_61_out, not_62_out, not_63_out, not_64_out, not_65_out, not_66_out,
       not_67_out, not_68_out, not_69_out, not_70_out, not_71_out, not_72_out, not_73_out, not_74_out,
       not_75_out, not_76_out, not_77_out, not_78_out, not_79_out, not_80_out, not_81_out, not_82_out,
       not_83_out, not_84_out, not_85_out, not_86_out, not_87_out, not_88_out, not_89_out, not_90_out,
       not_91_out;

  not not_1 (not_1_out, ALU0);
  not not_2 (not_2_out, F5);
  not not_3 (not_3_out, F4);
  not not_4 (not_4_out, F3);
  not not_5 (not_5_out, F2);
  not not_6 (not_6_out, F0);
  not not_7 (not_7_out, ALU0);
  not not_8 (not_8_out, F5);
  not not_9 (not_9_out, F4);
  not not_10 (not_10_out, F2);
  not not_11 (not_11_out, F1);
  not not_12 (not_12_out, ALU0);
  not not_13 (not_13_out, F2);
  not not_14 (not_14_out, F0);
  not not_15 (not_15_out, ALU1);
  not not_16 (not_16_out, ALU0);
  not not_17 (not_17_out, F3);
  not not_18 (not_18_out, F2);
  not not_19 (not_19_out, F1);
  not not_20 (not_20_out, F0);
  not not_21 (not_21_out, ALU1);
  not not_22 (not_22_out, F3);
  not not_23 (not_23_out, F1);
  not not_24 (not_24_out, ALU0);
  not not_25 (not_25_out, F2);
  not not_26 (not_26_out, F1);
  not not_27 (not_27_out, F0);
  not not_28 (not_28_out, ALU0);
  not not_29 (not_29_out, F3);
  not not_30 (not_30_out, ALU1);
  not not_31 (not_31_out, ALU0);
  not not_32 (not_32_out, F3);
  not not_33 (not_33_out, ALU0);
  not not_34 (not_34_out, F5);
  not not_35 (not_35_out, F4);
  not not_36 (not_36_out, F3);
  not not_37 (not_37_out, F2);
  not not_38 (not_38_out, ALU0);
  not not_39 (not_39_out, F2);
  not not_40 (not_40_out, ALU1);
  not not_41 (not_41_out, ALU0);
  not not_42 (not_42_out, F5);
  not not_43 (not_43_out, F1);
  not not_44 (not_44_out, ALU1);
  not not_45 (not_45_out, ALU0);
  not not_46 (not_46_out, F4);
  not not_47 (not_47_out, F0);
  not not_48 (not_48_out, ALU1);
  not not_49 (not_49_out, ALU0);
  not not_50 (not_50_out, F3);
  not not_51 (not_51_out, ALU0);
  not not_52 (not_52_out, F1);
  not not_53 (not_53_out, ALU1);
  not not_54 (not_54_out, ALU0);
  not not_55 (not_55_out, F0);
  not not_56 (not_56_out, ALU0);
  not not_57 (not_57_out, F2);
  not not_58 (not_58_out, F1);
  not not_59 (not_59_out, F0);
  not not_60 (not_60_out, ALU0);
  not not_61 (not_61_out, F2);
  not not_62 (not_62_out, ALU0);
  not not_63 (not_63_out, F4);
  not not_64 (not_64_out, F2);
  not not_65 (not_65_out, F1);
  not not_66 (not_66_out, ALU0);
  not not_67 (not_67_out, F3);
  not not_68 (not_68_out, F2);
  not not_69 (not_69_out, F1);
  not not_70 (not_70_out, F2);
  not not_71 (not_71_out, F1);
  not not_72 (not_72_out, F2);
  not not_73 (not_73_out, F1);
  not not_74 (not_74_out, ALU0);
  not not_75 (not_75_out, F5);
  not not_76 (not_76_out, F4);
  not not_77 (not_77_out, F3);
  not not_78 (not_78_out, F2);
  not not_79 (not_79_out, F1);
  not not_80 (not_80_out, F0);
  not not_81 (not_81_out, ALU1);
  not not_82 (not_82_out, ALU0);
  not not_83 (not_83_out, F3);
  not not_84 (not_84_out, F2);
  not not_85 (not_85_out, ALU0);
  not not_86 (not_86_out, ALU1);
  not not_87 (not_87_out, ALU0);
  not not_88 (not_88_out, F3);
  not not_89 (not_89_out, F2);
  not not_90 (not_90_out, F1);
  not not_91 (not_91_out, F0);
  and and_1 (and_1_out, not_1_out, not_2_out, not_3_out, not_4_out, not_5_out, not_6_out);
  and and_2 (and_2_out, not_7_out, not_8_out, not_9_out, F3, not_10_out, not_11_out, F0);
  and and_3 (and_3_out, not_12_out, F3, not_13_out, F1, not_14_out);
  and and_4 (and_4_out, not_15_out, not_16_out, F4, not_17_out, not_18_out, not_19_out, not_20_out);
  and and_5 (and_5_out, not_21_out, ALU0, not_22_out, F2, not_23_out, F0);
  and and_6 (and_6_out, ALU1, not_24_out, F3);
  and and_7 (and_7_out, ALU1, F3, not_25_out);
  and and_8 (and_8_out, ALU1, F3, not_26_out);
  and and_9 (and_9_out, ALU1, F3, not_27_out);
  and and_10 (and_10_out, not_28_out, not_29_out, F0);
  and and_11 (and_11_out, not_30_out, not_31_out, not_32_out, F1);
  and and_12 (and_12_out, not_33_out, not_34_out, not_35_out, not_36_out, not_37_out, F1);
  and and_13 (and_13_out, not_38_out, not_39_out, F1, F0);
  and and_14 (and_14_out, not_40_out, not_41_out, not_42_out, F2, not_43_out);
  and and_15 (and_15_out, not_44_out, not_45_out, not_46_out, F2, not_47_out);
  and and_16 (and_16_out, not_48_out, not_49_out, not_50_out, F2);
  and and_17 (and_17_out, not_51_out, F2, not_52_out, F0);
  and and_18 (and_18_out, not_53_out, not_54_out, F2, F1, not_55_out);
  and and_19 (and_19_out, not_56_out, F3, not_57_out, not_58_out, not_59_out);
  and and_20 (and_20_out, not_60_out, F4, not_61_out, F0);
  and and_21 (and_21_out, not_62_out, F5, not_63_out, not_64_out, not_65_out);
  and and_22 (and_22_out, ALU1, not_66_out, F0);
  and and_23 (and_23_out, ALU1, not_67_out, F0);
  and and_24 (and_24_out, ALU1, not_68_out, F0);
  and and_25 (and_25_out, ALU1, not_69_out, F0);
  and and_26 (and_26_out, ALU1, F4, not_70_out, not_71_out);
  and and_27 (and_27_out, ALU1, ALU0, not_72_out, not_73_out);
  and and_28 (and_28_out, not_74_out, not_75_out, not_76_out, not_77_out, not_78_out, not_79_out, not_80_out);
  and and_29 (and_29_out, not_81_out, not_82_out, not_83_out, not_84_out, F1, F0);
  and and_30 (and_30_out, not_85_out, F3, F2, F1, F0);
  and and_31 (and_31_out, not_86_out, not_87_out, F4, not_88_out, not_89_out, not_90_out, not_91_out);
  and and_32 (and_32_out, ALU1, F2);
  or or_1 (Oper2, and_1_out, and_2_out, and_3_out, and_4_out, and_5_out, and_6_out, and_7_out, and_8_out, and_9_out);
  or or_2 (Oper0, and_28_out, and_29_out, and_30_out, and_31_out, and_32_out);
  or or_3 (Oper1, and_10_out, and_11_out, and_12_out, and_13_out, and_14_out, and_15_out, and_16_out, and_17_out, and_18_out, and_19_out, and_20_out, and_21_out, and_22_out, and_23_out, and_24_out, and_25_out, and_26_out, and_27_out);
endmodule
