// Logisim project PipelinedMips-Pipeline.circ as structural Verilog: 11 circuits, main circuit 32bit +/-
module main (
  output [4:0] out_1,
  output [2:0] out_2,
  output [31:0] out_3,
  output [31:0] out_4,
  output [31:0] out_5,
  output [2:0] out_6
);

  wire alu_1_zero, ALUSrc, Branch, Branch2, Clock, EX_MEM_RegWrite, ID_EX_MemRead, Jump, MEM_WB_RegWrite,
       MemRead, MemRead2, MemtoReg, MemtoReg2, MemWrite, MemWrite2, not_1_out, RegDst, register_14_q,
       register_15_q, register_16_q, register_17_q, register_19_q, register_20_q, register_22_q,
       register_31_q, RegWrite, stall, To_PC_Mux;
  wire [1:0] ForA, ForB, register_1_q;
  wire [4:0] EX_MEM_Rd, ID_EX_Rs, ID_EX_Rt, ID_EX_Rt_stall, IF_ID_Rs, IF_ID_Rt, MEM_WB_Rd, multiplexer_5_out,
       RD, register_12_q, Shamt;
  wire [5:0] Funct, Opcode;
  wire [7:0] bit_extender_1_out, bit_extender_3_out;
  wire [20:16] register_4_q;
  wire [29:0] register_1_q_2;
  wire [31:0] A, adder_1_out, adder_2_out, alu_1_aluresult, bit_extender_2_out, EX_MEM_For, ID_EX_RD1,
       ID_EX_RD2, MemData, multiplexer_1_out, PC__4, PC_Branch, ram_1_data, regfile_1_rddata1,
       regfile_1_rddata2, register_3_q, register_13_q, register_27_q, register_28_q, rom_1_data,
       shifter_1_out, To2ndM;

  Clock clock_1 (.out(Clock));
  Register #(.width(32)) register_1 (
    .D(multiplexer_1_out), .en(not_1_out), .Q({register_1_q_2, register_1_q}), .clk(Clock));  // open: clr
  not not_1 (not_1_out, stall);
  Multiplexer #(.width(32), .enable("false")) multiplexer_1 (
    .in0(adder_1_out), .in1(PC_Branch), .out(multiplexer_1_out), .sel(To_PC_Mux));
  Bit_Extender #(.in_width(30), .out_width(8)) bit_extender_1 (.in(register_1_q_2), .out(bit_extender_1_out));
  NewControl_TestingFun newcontrol_testingfun_1 (
    .Op5(Opcode[5]), .Op4(Opcode[4]), .Op3(Opcode[3]), .Op2(Opcode[2]), .Op1(Opcode[1]), .Op0(Opcode[0]),
    .Fun5(Funct[5]), .Fun4(Funct[4]), .Fun3(Funct[3]), .Fun2(Funct[2]), .Fun1(Funct[1]), .Fun0(Funct[0]),
    .RegDst(RegDst), .AlUSrc(ALUSrc), .MemtoReg(MemtoReg), .RegWrite(RegWrite), .MemRead(MemRead),
    .MemWrite(MemWrite), .Branch(Branch), .Jump(Jump), .AluCtr0(out_6[2]), .AluCtr1(out_6[1]),
    .AluCtr2(out_6[0]));
  Forward forward_1 (
    .MEM_WB_RegWrite(MEM_WB_RegWrite), .EX_MEM_RegWrite(EX_MEM_RegWrite), .EX_MEM_Rd(EX_MEM_Rd),
    .MEM_WB_Rd(MEM_WB_Rd), .ID_EX_Rs(ID_EX_Rs), .ID_EX_Rt(ID_EX_Rt), .ForwardA(ForA), .ForwardB(ForB));
  Stall stall_1 (
    .ID_EX_MemRead(ID_EX_MemRead), .ID_EX_Rt(ID_EX_Rt_stall), .IF_ID_Rs(IF_ID_Rs), .IF_ID_Rt(IF_ID_Rt),
    .Opcode(Opcode), .stall(stall));
  Adder #(.width(32)) adder_1 (.a(32'h4), .b({register_1_q_2, register_1_q}), .out(adder_1_out));  // open: cin, cout
  Register #(.width(32)) register_2 (.D(32'h400), .clk(Clock));  // open: en, Q, clr
  ROM #(.dataWidth(32)) rom_1 (.addr(bit_extender_1_out), .data(rom_1_data));  // open: sel
  Register #(.width(32)) register_3 (.D(adder_1_out), .Q(register_3_q), .clk(Clock));  // open: en, clr
  Register #(.width(32)) register_4 (
    .D(rom_1_data), .Q({Opcode, IF_ID_Rs, register_4_q, RD, Shamt, Funct}), .clk(Clock));  // open: en, clr
  Multiplexer #(.select(2), .width(32), .enable("false")) multiplexer_2 (
    .in0(ID_EX_RD2), .in1(out_4), .in2(EX_MEM_For), .out(To2ndM), .sel(ForB));  // open: in3
  Register #(.width(5)) register_5 (.D(Shamt), .Q(out_1), .clk(Clock));  // open: en, clr
  Register #(.width(5)) register_6 (.D(IF_ID_Rs), .Q(ID_EX_Rs), .clk(Clock));  // open: en, clr
  Register #(.width(5)) register_7 (.D(IF_ID_Rt), .Q(ID_EX_Rt_stall), .clk(Clock));  // open: en, clr
  RegFile regfile_1 (
    .WrAddr(MEM_WB_Rd), .WrData(out_4), .WrReg(MEM_WB_RegWrite), .RdAddr1(IF_ID_Rs), .RdAddr2(register_4_q),
    .RdData1(regfile_1_rddata1), .RdData2(regfile_1_rddata2), .Clock(Clock));
  assign bit_extender_2_out = {{16{1'b0}}, {RD, Shamt, Funct}};  // Bit_Extender bit_extender_2
  Register #(.width(32)) register_8 (.D(register_3_q), .Q(PC__4), .clk(Clock));  // open: en, clr
  Register #(.width(32)) register_9 (.D(regfile_1_rddata1), .Q(ID_EX_RD1), .clk(Clock));  // open: en, clr
  Register #(.width(32)) register_10 (.D(regfile_1_rddata2), .Q(ID_EX_RD2), .clk(Clock));  // open: en, clr
  Multiplexer #(.width(32), .enable("false")) multiplexer_3 (
    .in0(To2ndM), .in1(register_13_q), .out(out_3), .sel(register_15_q));
  Register #(.width(5)) register_11 (.D(register_4_q), .Q(ID_EX_Rt), .clk(Clock));  // open: en, clr
  Register #(.width(5)) register_12 (.D(RD), .Q(register_12_q), .clk(Clock));  // open: en, clr
  Register #(.width(32)) register_13 (.D(bit_extender_2_out), .Q(register_13_q), .clk(Clock));  // open: en, clr
  Register #(.width(1)) register_14 (.D(RegDst), .Q(register_14_q), .clk(Clock));  // open: en, clr
  Register #(.width(1)) register_15 (.D(ALUSrc), .Q(register_15_q), .clk(Clock));  // open: en, clr
  Register #(.width(1)) register_16 (.D(MemtoReg), .Q(register_16_q), .clk(Clock));  // open: en, clr
  Register #(.width(1)) register_17 (.D(RegWrite), .Q(register_17_q), .clk(Clock));  // open: en, clr
  Register #(.width(1)) register_18 (.D(MemRead), .Q(ID_EX_MemRead), .clk(Clock));  // open: en, clr
  Register #(.width(1)) register_19 (.D(MemWrite), .Q(register_19_q), .clk(Clock));  // open: en, clr
  Register #(.width(1)) register_20 (.D(Branch), .Q(register_20_q), .clk(Clock));  // open: en, clr
  Register #(.width(3)) register_21 (.D(out_6), .Q(out_2), .clk(Clock));  // open: en, clr
  ALU alu_1 (
    .ALUCtl(out_2), .A(A), .B(out_3), .ALUResult(alu_1_aluresult), .Zero(alu_1_zero), .Shamt(out_1));  // open: Overflow
  Multiplexer #(.select(2), .width(32), .enable("false")) multiplexer_4 (
    .in0(ID_EX_RD1), .in1(out_4), .in2(EX_MEM_For), .out(A), .sel(ForA));  // open: in3
  Multiplexer #(.width(5), .enable("false")) multiplexer_5 (
    .in0(ID_EX_Rt), .in1(register_12_q), .out(multiplexer_5_out), .sel(register_14_q));
  Shifter #(.width(32)) shifter_1 (.in(register_13_q), .\dist (5'b00010), .out(shifter_1_out));
  Adder #(.width(32)) adder_2 (.a(shifter_1_out), .b(PC__4), .out(adder_2_out));  // open: cin, cout
  Register #(.width(1)) register_22 (.D(alu_1_zero), .Q(register_22_q), .clk(Clock));  // open: en, clr
  Register #(.width(32)) register_23 (.D(alu_1_aluresult), .Q(EX_MEM_For), .clk(Clock));  // open: en, clr
  Register #(.width(32)) register_24 (.D(To2ndM), .Q(MemData), .clk(Clock));  // open: en, clr
  Register #(.width(5)) register_25 (.D(multiplexer_5_out), .Q(EX_MEM_Rd), .clk(Clock));  // open: en, clr
  Register #(.width(32)) register_26 (.D(adder_2_out), .Q(PC_Branch), .clk(Clock));  // open: en, clr
  and and_1 (To_PC_Mux, register_22_q, Branch2);
  Bit_Extender #(.in_width(32), .out_width(8)) bit_extender_3 (.in(EX_MEM_For), .out(bit_extender_3_out));
  RAM #(.dataWidth(32), .bus("separate")) ram_1 (
    .addr(bit_extender_3_out), .din(MemData), .data(ram_1_data), .str(MemWrite2), .clk(Clock), .ld(MemRead2));  // open: sel, clr
  Register #(.width(32)) register_27 (.D(ram_1_data), .Q(register_27_q), .clk(Clock));  // open: en, clr
  Register #(.width(32)) register_28 (.D(EX_MEM_For), .Q(register_28_q), .clk(Clock));  // open: en, clr
  Register #(.width(5)) register_29 (.D(EX_MEM_Rd), .Q(MEM_WB_Rd), .clk(Clock));  // open: en, clr
  Register #(.width(32)) register_30 (.clk(Clock));  // open: D, en, Q, clr
  Register #(.width(1)) register_31 (.D(register_16_q), .Q(register_31_q), .clk(Clock));  // open: en, clr
  Register #(.width(1)) register_32 (.D(register_17_q), .Q(EX_MEM_RegWrite), .clk(Clock));  // open: en, clr
  Register #(.width(1)) register_33 (.D(ID_EX_MemRead), .Q(MemRead2), .clk(Clock));  // open: en, clr
  Register #(.width(1)) register_34 (.D(register_19_q), .Q(MemWrite2), .clk(Clock));  // open: en, clr
  Register #(.width(1)) register_35 (.D(register_20_q), .Q(Branch2), .clk(Clock));  // open: en, clr
  Multiplexer #(.width(32), .enable("false")) multiplexer_6 (
    .in0(register_28_q), .in1(register_27_q), .out(out_4), .sel(MemtoReg2));
  Register #(.width(1)) register_36 (.D(register_31_q), .Q(MemtoReg2), .clk(Clock));  // open: en, clr
  Register #(.width(1)) register_37 (.D(EX_MEM_RegWrite), .Q(MEM_WB_RegWrite), .clk(Clock));  // open: en, clr
  // Probe on nothing
  // Probe on nothing
  // Probe on nothing
  // Probe on nothing
  // Probe on nothing
  // Probe on nothing
  // Probe on nothing
  // Probe on nothing
  // Probe on nothing
  // Probe on nothing

  // Other names for the same wires on the sheet: RS[4:0] = IF_ID_Rs; ALU_Control_Sig2[2:0] = out_2;
  //   ALUControlSig[2:0] = out_6; RegWrite2 = MEM_WB_RegWrite; RT[4:0] = IF_ID_Rt; Shamt2[4:0] = out_1;
  //   WrAddr[4:0] = MEM_WB_Rd; WrData[31:0] = out_4

  // Notes on the sheet:
  //   PC
  //   contents of rom_1 (hex, n*v repeats v):
  //   34010001 211020 221822 2064000b 232824 aca4000a 8ca6000a c43824 10e10003 c7402a 11080001 201cffff
  //   8caa000a ad4afff7 8caa000a 1141fffc c000012 201bffff 23ff0018 ac1f0000 8c150000 2a00008 201affff
  //   8000017 20230000 20440000 20050001 a03020 10800006 ac650000 20840001 20630001 862022 10800001
  //   800001d 3e00008
  //   IF/ID
  //   PC
  //   Instr
  //   PC
  //   Rd
  //   Imm
  //   ID/EX
  //   Rt
  //   Controls Store ID/EX
  //   To Mux Rt/Rd
  //   To Mux RdData2/Imm
  //   EX/EM
  //   RdData2-2
  //   WrAdrr
  //   PC Branch
  //   MemRead2
  //   MemWrite2
  //   Branch2
  //   MEM/WB
  //   PC Branch
  //   Controls Store EX/MEM
  //   Controls Store MEM/WB
endmodule

module _32bit (
  input  Add_Sub_control,
  input  [31:0] in_2,
  input  [31:0] in_3,
  output [31:0] out_4,
  output carry_out
);

  wire adder_1_cout, subtractor_1_bout;
  wire [31:0] adder_1_out, subtractor_1_out;

  Adder #(.width(32)) adder_1 (.a(in_2), .b(in_3), .out(adder_1_out), .cout(adder_1_cout));  // open: cin
  Subtractor #(.width(32)) subtractor_1 (
    .a(in_2), .b(in_3), .out(subtractor_1_out), .bout(subtractor_1_bout));  // open: bin
  Multiplexer #(.width(32), .enable("false")) multiplexer_1 (
    .in0(adder_1_out), .in1(subtractor_1_out), .out(out_4), .sel(Add_Sub_control));
  Multiplexer #(.enable("false")) multiplexer_2 (
    .in0(adder_1_cout), .in1(subtractor_1_bout), .out(carry_out), .sel(Add_Sub_control));
endmodule

module ALU (
  input  [2:0] ALUCtl,
  input  [31:0] A,
  input  [31:0] B,
  input  [4:0] Shamt,
  output [31:0] ALUResult,
  output Zero,
  output Overflow
);

  wire and_2_out, and_3_out, comparator_1_lt, not_1_out, not_2_out, not_3_out, not_4_out, not_5_out, or_2_out;
  wire [31:0] Add, And, LessThan, Nor, Or, ShiftLeft, ShiftRight, Sub, Xor;

  Adder #(.width(32)) adder_1 (.a(A), .b(B), .out(Add));  // open: cin, cout
  Subtractor #(.width(32)) subtractor_1 (.a(A), .b(B), .out(Sub));  // open: bin, bout
  assign And = A & B;  // AND_Gate and_1, 32 bits wide
  assign Or = A | B;  // OR_Gate or_1, 32 bits wide
  assign Nor = ~(A | B);  // NOR_Gate nor_1, 32 bits wide
  Comparator #(.width(32)) comparator_1 (.a(A), .b(B), .lt(comparator_1_lt));  // open: gt, eq
  assign LessThan = {{31{1'b0}}, comparator_1_lt};  // Bit_Extender bit_extender_1
  Shifter #(.width(32)) shifter_1 (.in(B), .\dist (Shamt), .out(ShiftLeft));
  Shifter #(.width(32), .shift("lr")) shifter_2 (.in(B), .\dist (Shamt), .out(ShiftRight));
  not not_1 (not_1_out, ALUCtl[0]);
  not not_2 (not_2_out, ALUCtl[1]);
  not not_3 (not_3_out, ALUCtl[2]);
  not not_4 (not_4_out, ALUCtl[0]);
  not not_5 (not_5_out, ALUCtl[2]);
  and and_2 (and_2_out, not_1_out, not_2_out, not_3_out);
  and and_3 (and_3_out, not_4_out, ALUCtl[1], not_5_out);
  Multiplexer #(.select(3), .width(32), .enable("false")) multiplexer_1 (
    .in0(Sub), .in1(And), .in2(Add), .in3(Or), .in4(LessThan), .in5(ShiftLeft), .in6(ShiftRight), .in7(Xor),
    .out(ALUResult), .sel(ALUCtl));
  Overflow overflow_1 (
    .Add(and_3_out), .Sub(and_2_out), .ASign(A[31]), .BSign(B[31]), .ResultSign(ALUResult[31]),
    .Overflow(Overflow));
  not not_6 (Zero, or_2_out);
  or or_2 (or_2_out, ALUResult[0], ALUResult[1], ALUResult[2], ALUResult[3], ALUResult[4], ALUResult[5], ALUResult[6], ALUResult[7], ALUResult[8], ALUResult[9], ALUResult[10], ALUResult[11], ALUResult[12], ALUResult[13], ALUResult[14], ALUResult[15], ALUResult[16], ALUResult[17], ALUResult[18], ALUResult[19], ALUResult[20], ALUResult[21], ALUResult[22], ALUResult[23], ALUResult[24], ALUResult[25], ALUResult[26], ALUResult[27], ALUResult[28], ALUResult[29], ALUResult[30], ALUResult[31]);

  // Other names for the same wires on the sheet: ASign = A[31]; ResultSign = ALUResult[31]; BSign = B[31]
endmodule

module RegFile (
  input  [4:0] WrAddr,
  input  [31:0] WrData,
  input  WrReg,
  input  [4:0] RdAddr1,
  input  [4:0] RdAddr2,
  input  Clock,
  output [31:0] RdData1,
  output [31:0] RdData2
);

  wire and_1_out, and_2_out, comparator_1_eq, comparator_2_eq, comparator_3_eq, comparator_4_eq, not_1_out,
       not_2_out, WrReg0, WrReg1, WrReg2, WrReg3, WrReg4, WrReg5, WrReg6, WrReg7, WrReg8, WrReg9, WrReg10,
       WrReg11, WrReg12, WrReg13, WrReg14, WrReg15, WrReg16, WrReg17, WrReg18, WrReg19, WrReg20, WrReg21,
       WrReg22, WrReg23, WrReg24, WrReg25, WrReg26, WrReg27, WrReg28, WrReg29, WrReg30, WrReg31;
  wire [31:0] multiplexer_1_out, multiplexer_2_out, RegData1, RegData2, RegData3, RegData4, RegData5,
       RegData6, RegData7, RegData8, RegData9, RegData10, RegData11, RegData12, RegData13, RegData14,
       RegData15, RegData16, RegData17, RegData18, RegData19, RegData20, RegData21, RegData22, RegData23,
       RegData24, RegData25, RegData26, RegData27, RegData28, RegData29, RegData30, RegData31;

  Demultiplexer #(.select(5), .enable("false")) demultiplexer_1 (
    .out0(WrReg0), .out1(WrReg1), .out2(WrReg2), .out3(WrReg3), .out4(WrReg4), .out5(WrReg5), .out6(WrReg6),
    .out7(WrReg7), .out8(WrReg8), .out9(WrReg9), .out10(WrReg10), .out11(WrReg11), .out12(WrReg12),
    .out13(WrReg13), .out14(WrReg14), .out15(WrReg15), .out16(WrReg16), .out17(WrReg17), .out18(WrReg18),
    .out19(WrReg19), .out20(WrReg20), .out21(WrReg21), .out22(WrReg22), .out23(WrReg23), .out24(WrReg24),
    .out25(WrReg25), .out26(WrReg26), .out27(WrReg27), .out28(WrReg28), .out29(WrReg29), .out30(WrReg30),
    .out31(WrReg31), .in(WrReg), .sel(WrAddr));
  Register #(.width(32)) Reg4 (.D(WrData), .en(WrReg4), .Q(RegData4), .clk(Clock));  // open: clr
  Register #(.width(32)) Reg8 (.D(WrData), .en(WrReg8), .Q(RegData8), .clk(Clock));  // open: clr
  Register #(.width(32)) Reg12 (.D(WrData), .en(WrReg12), .Q(RegData12), .clk(Clock));  // open: clr
  Register #(.width(32)) Reg16 (.D(WrData), .en(WrReg16), .Q(RegData16), .clk(Clock));  // open: clr
  Register #(.width(32)) Reg20 (.D(WrData), .en(WrReg20), .Q(RegData20), .clk(Clock));  // open: clr
  Register #(.width(32)) Reg24 (.D(WrData), .en(WrReg24), .Q(RegData24), .clk(Clock));  // open: clr
  Register #(.width(32)) Reg28 (.D(WrData), .en(WrReg28), .Q(RegData28), .clk(Clock));  // open: clr
  Register #(.width(32)) Reg1 (.D(WrData), .en(WrReg1), .Q(RegData1), .clk(Clock));  // open: clr
  Register #(.width(32)) Reg5 (.D(WrData), .en(WrReg5), .Q(RegData5), .clk(Clock));  // open: clr
  Register #(.width(32)) Reg9 (.D(WrData), .en(WrReg9), .Q(RegData9), .clk(Clock));  // open: clr
  Register #(.width(32)) Reg13 (.D(WrData), .en(WrReg13), .Q(RegData13), .clk(Clock));  // open: clr
  Register #(.width(32)) Reg17 (.D(WrData), .en(WrReg17), .Q(RegData17), .clk(Clock));  // open: clr
  Register #(.width(32)) Reg21 (.D(WrData), .en(WrReg21), .Q(RegData21), .clk(Clock));  // open: clr
  Register #(.width(32)) Reg25 (.D(WrData), .en(WrReg25), .Q(RegData25), .clk(Clock));  // open: clr
  Register #(.width(32)) Reg29 (.D(WrData), .en(WrReg29), .Q(RegData29), .clk(Clock));  // open: clr
  Register #(.width(32)) Reg2 (.D(WrData), .en(WrReg2), .Q(RegData2), .clk(Clock));  // open: clr
  Register #(.width(32)) Reg6 (.D(WrData), .en(WrReg6), .Q(RegData6), .clk(Clock));  // open: clr
  Register #(.width(32)) Reg10 (.D(WrData), .en(WrReg10), .Q(RegData10), .clk(Clock));  // open: clr
  Register #(.width(32)) Reg14 (.D(WrData), .en(WrReg14), .Q(RegData14), .clk(Clock));  // open: clr
  Register #(.width(32)) Reg18 (.D(WrData), .en(WrReg18), .Q(RegData18), .clk(Clock));  // open: clr
  Register #(.width(32)) Reg22 (.D(WrData), .en(WrReg22), .Q(RegData22), .clk(Clock));  // open: clr
  Register #(.width(32)) Reg26 (.D(WrData), .en(WrReg26), .Q(RegData26), .clk(Clock));  // open: clr
  Register #(.width(32)) Reg30 (.D(WrData), .en(WrReg30), .Q(RegData30), .clk(Clock));  // open: clr
  Register #(.width(32)) Reg3 (.D(WrData), .en(WrReg3), .Q(RegData3), .clk(Clock));  // open: clr
  Register #(.width(32)) Reg7 (.D(WrData), .en(WrReg7), .Q(RegData7), .clk(Clock));  // open: clr
  Register #(.width(32)) Reg11 (.D(WrData), .en(WrReg11), .Q(RegData11), .clk(Clock));  // open: clr
  Register #(.width(32)) Reg15 (.D(WrData), .en(WrReg15), .Q(RegData15), .clk(Clock));  // open: clr
  Register #(.width(32)) Reg19 (.D(WrData), .en(WrReg19), .Q(RegData19), .clk(Clock));  // open: clr
  Register #(.width(32)) Reg23 (.D(WrData), .en(WrReg23), .Q(RegData23), .clk(Clock));  // open: clr
  Register #(.width(32)) Reg27 (.D(WrData), .en(WrReg27), .Q(RegData27), .clk(Clock));  // open: clr
  Register #(.width(32)) Reg31 (.D(WrData), .en(WrReg31), .Q(RegData31), .clk(Clock));  // open: clr
  Multiplexer #(.select(5), .width(32), .enable("false")) multiplexer_1 (
    .in0({32{1'b0}}), .in1(RegData1), .in2(RegData2), .in3(RegData3), .in4(RegData4), .in5(RegData5),
    .in6(RegData6), .in7(RegData7), .in8(RegData8), .in9(RegData9), .in10(RegData10), .in11(RegData11),
    .in12(RegData12), .in13(RegData13), .in14(RegData14), .in15(RegData15), .in16(RegData16),
    .in17(RegData17), .in18(RegData18), .in19(RegData19), .in20(RegData20), .in21(RegData21),
    .in22(RegData22), .in23(RegData23), .in24(RegData24), .in25(RegData25), .in26(RegData26),
    .in27(RegData27), .in28(RegData28), .in29(RegData29), .in30(RegData30), .in31(RegData31),
    .out(multiplexer_1_out), .sel(RdAddr1));
  Multiplexer #(.select(5), .width(32), .enable("false")) multiplexer_2 (
    .in0({32{1'b0}}), .in1(RegData1), .in2(RegData2), .in3(RegData3), .in4(RegData4), .in5(RegData5),
    .in6(RegData6), .in7(RegData7), .in8(RegData8), .in9(RegData9), .in10(RegData10), .in11(RegData11),
    .in12(RegData12), .in13(RegData13), .in14(RegData14), .in15(RegData15), .in16(RegData16),
    .in17(RegData17), .in18(RegData18), .in19(RegData19), .in20(RegData20), .in21(RegData21),
    .in22(RegData22), .in23(RegData23), .in24(RegData24), .in25(RegData25), .in26(RegData26),
    .in27(RegData27), .in28(RegData28), .in29(RegData29), .in30(RegData30), .in31(RegData31),
    .out(multiplexer_2_out), .sel(RdAddr2));
  Multiplexer #(.width(32), .enable("false")) multiplexer_3 (
    .in0(multiplexer_1_out), .in1(WrData), .out(RdData1), .sel(and_1_out));
  Multiplexer #(.width(32), .enable("false")) multiplexer_4 (
    .in0(multiplexer_2_out), .in1(WrData), .out(RdData2), .sel(and_2_out));
  Comparator #(.width(5), .mode("unsigned")) comparator_1 (
    .a(WrAddr), .b(RdAddr1), .eq(comparator_1_eq));  // open: gt, lt
  and and_1 (and_1_out, comparator_1_eq, WrReg, not_1_out);
  Comparator #(.width(5), .mode("unsigned")) comparator_2 (
    .a(WrAddr), .b(RdAddr2), .eq(comparator_2_eq));  // open: gt, lt
  and and_2 (and_2_out, comparator_2_eq, WrReg, not_2_out);
  Comparator #(.width(5), .mode("unsigned")) comparator_3 (
    .a(WrAddr), .b({5{1'b0}}), .eq(comparator_3_eq));  // open: gt, lt
  not not_1 (not_1_out, comparator_3_eq);
  Comparator #(.width(5), .mode("unsigned")) comparator_4 (
    .a(WrAddr), .b({5{1'b0}}), .eq(comparator_4_eq));  // open: gt, lt
  not not_2 (not_2_out, comparator_4_eq);
endmodule

module Overflow (
  input  Add,
  input  Sub,
  input  ASign,
  input  BSign,
  input  ResultSign,
  output Overflow
);

  wire and_1_out, and_2_out, or_1_out, xnor_1_out, xor_1_out, xor_2_out;

  xnor xnor_1 (xnor_1_out, ASign, BSign);
  xor xor_1 (xor_1_out, ASign, BSign);
  and and_1 (and_1_out, xnor_1_out, Add);
  and and_2 (and_2_out, xor_1_out, Sub);
  or or_1 (or_1_out, and_1_out, and_2_out);
  xor xor_2 (xor_2_out, ResultSign, ASign);
  and and_3 (Overflow, or_1_out, xor_2_out);

  // Notes on the sheet:
  //   Overflow occurs when doing addition and sign(A) == sign(B) && sign(result) != sign(A)
  //   Or
  //   Overflow occurs when doing subtraction and sign(A) != sign(B) && sign(result) != sign(A)
endmodule

module NewControl (
  input  Op5,
  input  Op4,
  input  Op3,
  input  Op2,
  input  Op1,
  input  Op0,
  output RegDst,
  output AlUSrc,
  output MemtoReg,
  output RegWrite,
  output MemRead,
  output MemWrite,
  output Branch,
  output ALUOp1,
  output AlUOp0,
  output Jump
);

  wire and_3_out, and_4_out, and_7_out, and_8_out, and_9_out, and_10_out, and_11_out, and_12_out, and_13_out,
       and_14_out, not_1_out, not_2_out, not_3_out, not_4_out, not_5_out, not_6_out, not_7_out, not_8_out,
       not_9_out, not_10_out, not_11_out, not_12_out, not_13_out, not_14_out, not_15_out, not_16_out,
       not_17_out, not_18_out, not_19_out, not_20_out, not_21_out, not_22_out, not_23_out, not_24_out,
       not_25_out, not_26_out, not_27_out;

  not not_1 (not_1_out, Op3);
  not not_2 (not_2_out, Op1);
  or or_1 (AlUSrc, Op0, Op3);
  not not_3 (not_3_out, Op3);
  not not_4 (not_4_out, Op2);
  not not_5 (not_5_out, Op5);
  not not_6 (not_6_out, Op3);
  and and_1 (MemWrite, Op5, Op3);
  not not_7 (not_7_out, Op3);
  not not_8 (not_8_out, Op5);
  not not_9 (not_9_out, Op3);
  not not_10 (not_10_out, Op2);
  not not_11 (not_11_out, Op5);
  not not_12 (not_12_out, Op2);
  not not_13 (not_13_out, Op1);
  not not_14 (not_14_out, Op5);
  not not_15 (not_15_out, Op2);
  not not_16 (not_16_out, Op5);
  not not_17 (not_17_out, Op5);
  not not_18 (not_18_out, Op2);
  not not_19 (not_19_out, Op0);
  not not_20 (not_20_out, Op5);
  not not_21 (not_21_out, Op4);
  not not_22 (not_22_out, Op3);
  not not_23 (not_23_out, Op2);
  not not_24 (not_24_out, Op5);
  not not_25 (not_25_out, Op4);
  not not_26 (not_26_out, Op2);
  not not_27 (not_27_out, Op1);
  and and_2 (RegDst, not_1_out, not_2_out);
  and and_3 (and_3_out, not_3_out, not_4_out);
  and and_4 (and_4_out, not_5_out, Op3);
  and and_5 (MemRead, not_6_out, Op0);
  and and_6 (Branch, not_7_out, Op2);
  and and_7 (and_7_out, not_8_out, not_9_out, not_10_out);
  and and_8 (and_8_out, not_11_out, not_12_out, not_13_out);
  and and_9 (and_9_out, not_14_out, not_15_out, Op0);
  and and_10 (and_10_out, not_16_out, Op3, Op2);
  and and_11 (and_11_out, not_17_out, Op4, not_18_out);
  and and_12 (and_12_out, Op3, not_19_out);
  and and_13 (and_13_out, not_20_out, not_21_out, not_22_out, not_23_out, Op1);
  and and_14 (and_14_out, not_24_out, not_25_out, Op3, not_26_out, not_27_out, Op0);
  or or_2 (RegWrite, and_3_out, and_4_out);
  or or_3 (ALUOp1, and_7_out, and_8_out, and_9_out, and_10_out, and_11_out);
  or or_4 (AlUOp0, Op2, and_12_out);
  or or_5 (Jump, and_13_out, and_14_out);

  assign MemtoReg = Op5;
endmodule

module NewALU (
  input  ALU1,
  input  ALU0,
  input  F5,
  input  F4,
  input  F3,
  input  F2,
  input  F1,
  input  F0,
  output Oper2,
  output Oper1,
  output Oper0
);

  wire and_1_out, and_2_out, and_3_out, and_4_out, and_5_out, and_6_out, and_7_out, and_8_out, and_9_out,
       and_10_out, and_11_out, and_12_out, and_13_out, and_14_out, and_15_out, and_16_out, and_17_out,
       and_18_out, and_19_out, and_20_out, and_21_out, and_22_out, and_23_out, and_24_out, and_25_out,
       and_26_out, and_27_out, and_28_out, and_29_out, and_30_out, and_31_out, and_32_out, and_33_out,
       and_34_out, and_35_out, and_36_out, and_37_out, and_38_out, and_39_out, and_40_out, and_41_out,
       and_42_out, and_43_out, not_1_out, not_2_out, not_3_out, not_4_out, not_5_out, not_6_out, not_7_out,
       not_8_out, not_9_out, not_10_out, not_11_out, not_12_out, not_13_out, not_14_out, not_15_out,
       not_16_out, not_17_out, not_18_out, not_19_out, not_20_out, not_21_out, not_22_out, not_23_out,
       not_24_out, not_25_out, not_26_out, not_27_out, not_28_out, not_29_out, not_30_out, not_31_out,
       not_32_out, not_33_out, not_34_out, not_35_out, not_36_out, not_37_out, not_38_out, not_39_out,
       not_40_out, not_41_out, not_42_out, not_43_out, not_44_out, not_45_out, not_46_out, not_47_out,
       not_48_out, not_49_out, not_50_out, not_51_out, not_52_out, not_53_out, not_54_out, not_55_out,
       not_56_out, not_57_out, not_58_out, not_59_out, not_60_out, not_61_out, not_62_out, not_63_out,
       not_64_out, not_65_out, not_66_out, not_67_out, not_68_out, not_69_out, not_70_out, not_71_out,
       not_72_out, not_73_out, not_74_out, not_75_out, not_76_out, not_77_out, not_78_out, not_79_out,
       not_80_out, not_81_out, not_82_out, not_83_out, not_84_out, not_85_out, not_86_out, not_87_out,
       not_88_out, not_89_out, not_90_out, not_91_out, not_92_out, not_93_out, not_94_out, not_95_out,
       not_96_out, not_97_out, not_98_out, not_99_out, not_100_out, not_101_out, not_102_out, not_103_out,
       not_104_out, not_105_out, not_106_out, not_107_out, not_108_out, not_109_out, not_110_out,
       not_111_out, not_112_out, not_113_out, not_114_out, not_115_out, not_116_out, not_117_out,
       not_118_out, not_119_out, not_120_out, not_121_out, not_122_out, not_123_out;

  not not_1 (not_1_out, ALU0);
  not not_2 (not_2_out, F5);
  not not_3 (not_3_out, F4);
  not not_4 (not_4_out, F3);
  not not_5 (not_5_out, F2);
  not not_6 (not_6_out, F0);
  not not_7 (not_7_out, ALU0);
  not not_8 (not_8_out, F5);
  not not_9 (not_9_out, F4);
  not not_10 (not_10_out, F2);
  not not_11 (not_11_out, F1);
  not not_12 (not_12_out, ALU1);
  not not_13 (not_13_out, ALU0);
  not not_14 (not_14_out, F3);
  not not_15 (not_15_out, F2);
  not not_16 (not_16_out, F1);
  not not_17 (not_17_out, F0);
  not not_18 (not_18_out, ALU0);
  not not_19 (not_19_out, F2);
  not not_20 (not_20_out, F0);
  not not_21 (not_21_out, ALU0);
  not not_22 (not_22_out, F2);
  not not_23 (not_23_out, F0);
  not not_24 (not_24_out, ALU1);
  not not_25 (not_25_out, F3);
  not not_26 (not_26_out, F1);
  not not_27 (not_27_out, ALU0);
  not not_28 (not_28_out, F2);
  not not_29 (not_29_out, F1);
  not not_30 (not_30_out, F0);
  not not_31 (not_31_out, ALU0);
  not not_32 (not_32_out, F3);
  not not_33 (not_33_out, ALU1);
  not not_34 (not_34_out, ALU0);
  not not_35 (not_35_out, F5);
  not not_36 (not_36_out, F4);
  not not_37 (not_37_out, F2);
  not not_38 (not_38_out, ALU1);
  not not_39 (not_39_out, ALU0);
  not not_40 (not_40_out, F3);
  not not_41 (not_41_out, ALU0);
  not not_42 (not_42_out, F5);
  not not_43 (not_43_out, F4);
  not not_44 (not_44_out, F3);
  not not_45 (not_45_out, F2);
  not not_46 (not_46_out, ALU1);
  not not_47 (not_47_out, ALU0);
  not not_48 (not_48_out, F5);
  not not_49 (not_49_out, F1);
  not not_50 (not_50_out, ALU1);
  not not_51 (not_51_out, ALU0);
  not not_52 (not_52_out, F0);
  not not_53 (not_53_out, ALU1);
  not not_54 (not_54_out, ALU0);
  not not_55 (not_55_out, F4);
  not not_56 (not_56_out, F1);
  not not_57 (not_57_out, F0);
  not not_58 (not_58_out, ALU0);
  not not_59 (not_59_out, F2);
  not not_60 (not_60_out, F1);
  not not_61 (not_61_out, F0);
  not not_62 (not_62_out, ALU0);
  not not_63 (not_63_out, F2);
  not not_64 (not_64_out, ALU1);
  not not_65 (not_65_out, ALU0);
  not not_66 (not_66_out, F3);
  not not_67 (not_67_out, ALU0);
  not not_68 (not_68_out, F4);
  not not_69 (not_69_out, F2);
  not not_70 (not_70_out, F1);
  not not_71 (not_71_out, ALU0);
  not not_72 (not_72_out, F2);
  not not_73 (not_73_out, ALU0);
  not not_74 (not_74_out, F1);
  not not_75 (not_75_out, F5);
  not not_76 (not_76_out, F4);
  not not_77 (not_77_out, F3);
  not not_78 (not_78_out, F2);
  not not_79 (not_79_out, F1);
  not not_80 (not_80_out, F0);
  not not_81 (not_81_out, ALU0);
  not not_82 (not_82_out, F3);
  not not_83 (not_83_out, F2);
  not not_84 (not_84_out, F1);
  not not_85 (not_85_out, F2);
  not not_86 (not_86_out, F1);
  not not_87 (not_87_out, F2);
  not not_88 (not_88_out, F1);
  not not_89 (not_89_out, F2);
  not not_90 (not_90_out, F1);
  not not_91 (not_91_out, F5);
  not not_92 (not_92_out, F4);
  not not_93 (not_93_out, F3);
  not not_94 (not_94_out, ALU0);
  not not_95 (not_95_out, F5);
  not not_96 (not_96_out, F4);
  not not_97 (not_97_out, F3);
  not not_98 (not_98_out, F2);
  not not_99 (not_99_out, F1);
  not not_100 (not_100_out, F0);
  not not_101 (not_101_out, ALU1);
  not not_102 (not_102_out, ALU0);
  not not_103 (not_103_out, F3);
  not not_104 (not_104_out, F2);
  not not_105 (not_105_out, ALU0);
  not not_106 (not_106_out, ALU1);
  not not_107 (not_107_out, ALU0);
  not not_108 (not_108_out, F3);
  not not_109 (not_109_out, F2);
  not not_110 (not_110_out, F1);
  not not_111 (not_111_out, F0);
  not not_112 (not_112_out, ALU0);
  not not_113 (not_113_out, F4);
  not not_114 (not_114_out, F3);
  not not_115 (not_115_out, F1);
  not not_116 (not_116_out, F0);
  not not_117 (not_117_out, ALU0);
  not not_118 (not_118_out, F1);
  not not_119 (not_119_out, F0);
  not not_120 (not_120_out, F5);
  not not_121 (not_121_out, F4);
  not not_122 (not_122_out, F3);
  not not_123 (not_123_out, F2);
  and and_1 (and_1_out, not_1_out, not_2_out, not_3_out, not_4_out, not_5_out, not_6_out);
  and and_2 (and_2_out, not_7_out, not_8_out, not_9_out, F3, not_10_out, not_11_out, F0);
  and and_3 (and_3_out, not_12_out, not_13_out, F4, not_14_out, not_15_out, not_16_out, not_17_out);
  and and_4 (and_4_out, not_18_out, F4, F3, not_19_out, F1, not_20_out);
  and and_5 (and_5_out, not_21_out, F5, F3, not_22_out, F1, not_23_out);
  and and_6 (and_6_out, not_24_out, ALU0, not_25_out, F2, not_26_out, F0);
  and and_7 (and_7_out, ALU1, not_27_out, F3);
  and and_8 (and_8_out, ALU1, F3, not_28_out);
  and and_9 (and_9_out, ALU1, F3, not_29_out);
  and and_10 (and_10_out, ALU1, F3, not_30_out);
  and and_11 (and_11_out, not_31_out, not_32_out, F0);
  and and_12 (and_12_out, not_33_out, not_34_out, not_35_out, not_36_out, not_37_out, F1);
  and and_13 (and_13_out, not_38_out, not_39_out, not_40_out, F1);
  and and_14 (and_14_out, not_41_out, not_42_out, not_43_out, not_44_out, not_45_out, F1);
  and and_15 (and_15_out, not_46_out, not_47_out, not_48_out, F2, not_49_out);
  and and_16 (and_16_out, not_50_out, not_51_out, F2, F1, not_52_out);
  and and_17 (and_17_out, not_53_out, not_54_out, not_55_out, F3, not_56_out, not_57_out);
  and and_18 (and_18_out, not_58_out, F3, not_59_out, not_60_out, not_61_out);
  and and_19 (and_19_out, not_62_out, F4, not_63_out, F0);
  and and_20 (and_20_out, not_64_out, not_65_out, F4, not_66_out, F2);
  and and_21 (and_21_out, not_67_out, F5, not_68_out, not_69_out, not_70_out);
  and and_22 (and_22_out, not_71_out, F5, not_72_out, F0);
  and and_23 (and_23_out, not_73_out, F5, not_74_out, F0);
  and and_24 (and_24_out, ALU0, not_75_out, not_76_out, not_77_out, not_78_out, not_79_out, not_80_out);
  and and_25 (and_25_out, ALU1, not_81_out, F0);
  and and_26 (and_26_out, ALU1, not_82_out, F0);
  and and_27 (and_27_out, ALU1, not_83_out, F0);
  and and_28 (and_28_out, ALU1, not_84_out, F0);
  and and_29 (and_29_out, ALU1, F3, not_85_out, not_86_out);
  and and_30 (and_30_out, ALU1, F4, not_87_out, not_88_out);
  and and_31 (and_31_out, ALU1, F5, not_89_out, not_90_out);
  and and_32 (and_32_out, ALU1, ALU0, not_91_out, not_92_out, not_93_out);
  and and_33 (and_33_out, not_94_out, not_95_out, not_96_out, not_97_out, not_98_out, not_99_out, not_100_out);
  and and_34 (and_34_out, not_101_out, not_102_out, not_103_out, not_104_out, F1, F0);
  and and_35 (and_35_out, not_105_out, F3, F2, F1, F0);
  and and_36 (and_36_out, not_106_out, not_107_out, F4, not_108_out, not_109_out, not_110_out, not_111_out);
  and and_37 (and_37_out, not_112_out, F5, not_113_out, not_114_out, F2, not_115_out, not_116_out);
  and and_38 (and_38_out, ALU1, not_117_out, F2);
  and and_39 (and_39_out, ALU1, F2, not_118_out, not_119_out);
  and and_40 (and_40_out, ALU1, F3, F2);
  and and_41 (and_41_out, ALU1, F4, F2);
  and and_42 (and_42_out, ALU1, F5, F2);
  and and_43 (and_43_out, ALU1, ALU0, not_120_out, not_121_out, not_122_out, not_123_out, F1, F0);
  or or_1 (Oper2, and_1_out, and_2_out, and_3_out, and_4_out, and_5_out, and_6_out, and_7_out, and_8_out, and_9_out, and_10_out);
  or or_2 (Oper0, and_33_out, and_34_out, and_35_out, and_36_out, and_37_out, and_38_out, and_39_out, and_40_out, and_41_out, and_42_out, and_43_out);
  or or_3 (Oper1, and_11_out, and_12_out, and_13_out, and_14_out, and_15_out, and_16_out, and_17_out, and_18_out, and_19_out, and_20_out, and_21_out, and_22_out, and_23_out, and_24_out, and_25_out, and_26_out, and_27_out, and_28_out, and_29_out, and_30_out, and_31_out, and_32_out);
endmodule

module NewControl_Testing7 (
  input  Op5,
  input  Op4,
  input  Op3,
  input  Op2,
  input  Op1,
  input  Op0,
  output RegDst,
  output AlUSrc,
  output MemtoReg,
  output RegWrite,
  output MemRead,
  output MemWrite,
  output Branch,
  output ALUOp1,
  output AlUOp0,
  output Jump
);

  wire and_3_out, and_4_out, and_5_out, and_6_out, and_7_out, and_8_out, and_9_out, and_10_out, and_11_out,
       and_12_out, and_13_out, and_14_out, and_15_out, and_16_out, and_18_out, and_19_out, and_20_out,
       and_21_out, and_22_out, and_23_out, and_24_out, and_25_out, and_26_out, and_27_out, not_1_out,
       not_2_out, not_3_out, not_4_out, not_5_out, not_6_out, not_7_out, not_8_out, not_9_out, not_10_out,
       not_11_out, not_12_out, not_13_out, not_14_out, not_15_out, not_16_out, not_17_out, not_18_out,
       not_19_out, not_20_out, not_21_out, not_22_out, not_23_out, not_24_out, not_25_out, not_26_out,
       not_27_out, not_28_out, not_29_out, not_30_out, not_31_out, not_32_out, not_33_out, not_34_out,
       not_35_out, not_36_out, not_37_out, not_38_out, not_39_out, not_40_out, not_41_out, not_42_out,
       not_43_out, not_44_out, not_45_out, not_46_out;

  not not_1 (not_1_out, Op3);
  not not_2 (not_2_out, Op1);
  or or_1 (AlUSrc, Op0, Op3);
  not not_3 (not_3_out, Op1);
  not not_4 (not_4_out, Op0);
  not not_5 (not_5_out, Op3);
  not not_6 (not_6_out, Op2);
  not not_7 (not_7_out, Op3);
  not not_8 (not_8_out, Op2);
  not not_9 (not_9_out, Op4);
  not not_10 (not_10_out, Op2);
  not not_11 (not_11_out, Op5);
  not not_12 (not_12_out, Op3);
  not not_13 (not_13_out, Op2);
  not not_14 (not_14_out, Op3);
  not not_15 (not_15_out, Op2);
  not not_16 (not_16_out, Op5);
  not not_17 (not_17_out, Op3);
  not not_18 (not_18_out, Op3);
  not not_19 (not_19_out, Op1);
  not not_20 (not_20_out, Op3);
  not not_21 (not_21_out, Op3);
  and and_1 (MemWrite, Op5, Op3);
  not not_22 (not_22_out, Op3);
  not not_23 (not_23_out, Op5);
  not not_24 (not_24_out, Op2);
  not not_25 (not_25_out, Op5);
  not not_26 (not_26_out, Op3);
  not not_27 (not_27_out, Op2);
  not not_28 (not_28_out, Op4);
  not not_29 (not_29_out, Op3);
  not not_30 (not_30_out, Op2);
  not not_31 (not_31_out, Op5);
  not not_32 (not_32_out, Op1);
  not not_33 (not_33_out, Op5);
  not not_34 (not_34_out, Op5);
  not not_35 (not_35_out, Op2);
  not not_36 (not_36_out, Op0);
  not not_37 (not_37_out, Op4);
  not not_38 (not_38_out, Op3);
  not not_39 (not_39_out, Op5);
  not not_40 (not_40_out, Op4);
  not not_41 (not_41_out, Op3);
  not not_42 (not_42_out, Op2);
  not not_43 (not_43_out, Op5);
  not not_44 (not_44_out, Op4);
  not not_45 (not_45_out, Op2);
  not not_46 (not_46_out, Op1);
  and and_2 (RegDst, not_1_out, not_2_out);
  and and_3 (and_3_out, Op5, not_3_out);
  and and_4 (and_4_out, Op5, not_4_out);
  and and_5 (and_5_out, Op5, Op2);
  and and_6 (and_6_out, Op5, Op4);
  and and_7 (and_7_out, not_5_out, not_6_out, Op0);
  and and_8 (and_8_out, not_7_out, not_8_out, Op1);
  and and_9 (and_9_out, not_9_out, not_10_out, Op1, Op0);
  and and_10 (and_10_out, not_11_out, Op3);
  and and_11 (and_11_out, Op4, not_12_out, not_13_out);
  and and_12 (and_12_out, Op5, not_14_out, not_15_out);
  and and_13 (and_13_out, not_16_out, not_17_out, Op0);
  and and_14 (and_14_out, not_18_out, not_19_out, Op0);
  and and_15 (and_15_out, not_20_out, Op2, Op0);
  and and_16 (and_16_out, Op4, not_21_out, Op0);
  and and_17 (Branch, not_22_out, Op2);
  and and_18 (and_18_out, not_23_out, not_24_out, Op0);
  and and_19 (and_19_out, not_25_out, not_26_out, not_27_out, Op1);
  and and_20 (and_20_out, not_28_out, not_29_out, not_30_out, Op1, Op0);
  and and_21 (and_21_out, not_31_out, Op3, not_32_out);
  and and_22 (and_22_out, not_33_out, Op3, Op2);
  and and_23 (and_23_out, not_34_out, Op4, not_35_out);
  and and_24 (and_24_out, Op3, not_36_out);
  and and_25 (and_25_out, Op5, not_37_out, not_38_out, Op1, Op0);
  and and_26 (and_26_out, not_39_out, not_40_out, not_41_out, not_42_out, Op1);
  and and_27 (and_27_out, not_43_out, not_44_out, Op3, not_45_out, not_46_out, Op0);
  or or_2 (MemtoReg, and_3_out, and_4_out, and_5_out, and_6_out);
  or or_3 (RegWrite, and_7_out, and_8_out, and_9_out, and_10_out, and_11_out, and_12_out);
  or or_4 (MemRead, and_13_out, and_14_out, and_15_out, and_16_out);
  or or_5 (ALUOp1, and_18_out, and_19_out, and_20_out, and_21_out, and_22_out, and_23_out);
  or or_6 (AlUOp0, Op2, and_24_out, and_25_out);
  or or_7 (Jump, and_26_out, and_27_out);
endmodule

module NewControl_TestingFun (
  input  Op5,
  input  Op4,
  input  Op3,
  input  Op2,
  input  Op1,
  input  Op0,
  input  Fun5,
  input  Fun4,
  input  Fun3,
  input  Fun2,
  input  Fun1,
  input  Fun0,
  output RegDst,
  output AlUSrc,
  output MemtoReg,
  output RegWrite,
  output MemRead,
  output MemWrite,
  output Branch,
  output Jump,
  output AluCtr0,
  output AluCtr1,
  output AluCtr2
);

  wire and_2_out, and_3_out, and_4_out, and_5_out, and_6_out, and_7_out, and_8_out, and_9_out, and_10_out,
       and_11_out, and_12_out, and_13_out, and_14_out, and_15_out, and_16_out, and_17_out, and_18_out,
       and_19_out, and_20_out, and_21_out, and_22_out, and_23_out, and_24_out, and_25_out, and_26_out,
       and_27_out, and_28_out, and_29_out, and_30_out, and_31_out, and_32_out, and_33_out, and_34_out,
       and_35_out, and_36_out, and_37_out, and_38_out, and_39_out, and_40_out, and_41_out, and_42_out,
       and_43_out, and_44_out, and_45_out, and_46_out, and_47_out, and_48_out, and_49_out, and_50_out,
       and_51_out, and_52_out, and_53_out, and_54_out, and_55_out, and_56_out, and_57_out, and_58_out,
       and_59_out, and_60_out, and_61_out, and_62_out, and_63_out, and_64_out, and_65_out, and_66_out,
       and_67_out, and_68_out, and_69_out, and_70_out, and_71_out, and_72_out, and_73_out, and_74_out,
       and_75_out, and_76_out, and_77_out, not_1_out, not_2_out, not_3_out, not_4_out, not_5_out, not_6_out,
       not_7_out, not_8_out, not_9_out, not_10_out, not_11_out, not_12_out, not_13_out, not_14_out,
       not_15_out, not_16_out, not_17_out, not_18_out, not_19_out, not_20_out, not_21_out, not_22_out,
       not_23_out, not_24_out, not_25_out, not_26_out, not_27_out, not_28_out, not_29_out, not_30_out,
       not_31_out, not_32_out, not_33_out, not_34_out, not_35_out, not_36_out, not_37_out, not_38_out,
       not_39_out, not_40_out, not_41_out, not_42_out, not_43_out, not_44_out, not_45_out, not_46_out,
       not_47_out, not_48_out, not_49_out, not_50_out, not_51_out, not_52_out, not_53_out, not_54_out,
       not_55_out, not_56_out, not_57_out, not_58_out, not_59_out, not_60_out, not_61_out, not_62_out,
       not_63_out, not_64_out, not_65_out, not_66_out, not_67_out, not_68_out, not_69_out, not_70_out,
       not_71_out, not_72_out, not_73_out, not_74_out, not_75_out, not_76_out, not_77_out, not_78_out,
       not_79_out, not_80_out, not_81_out, not_82_out, not_83_out, not_84_out, not_85_out, not_86_out,
       not_87_out, not_88_out, not_89_out, not_90_out, not_91_out, not_92_out, not_93_out, not_94_out,
       not_95_out, not_96_out, not_97_out, not_98_out, not_99_out, not_100_out, not_101_out, not_102_out,
       not_103_out, not_104_out, not_105_out, not_106_out, not_107_out, not_108_out, not_109_out,
       not_110_out, not_111_out, not_112_out, not_113_out, not_114_out, not_115_out, not_116_out,
       not_117_out, not_118_out, not_119_out, not_120_out, not_121_out, not_122_out, not_123_out,
       not_124_out, not_125_out, not_126_out, not_127_out, not_128_out, not_129_out, not_130_out,
       not_131_out, not_132_out, not_133_out, not_134_out, not_135_out, not_136_out, not_137_out,
       not_138_out, not_139_out, not_140_out, not_141_out, not_142_out, not_143_out, not_144_out,
       not_145_out, not_146_out, not_147_out, not_148_out, not_149_out, not_150_out, not_151_out,
       not_152_out, not_153_out, not_154_out, not_155_out, not_156_out, not_157_out, not_158_out,
       not_159_out, not_160_out, not_161_out, not_162_out, not_163_out, not_164_out, not_165_out,
       not_166_out, not_167_out, not_168_out, not_169_out, not_170_out, not_171_out, not_172_out,
       not_173_out, not_174_out, not_175_out, not_176_out, not_177_out, not_178_out, not_179_out,
       not_180_out, not_181_out, not_182_out, not_183_out, not_184_out, not_185_out, not_186_out,
       not_187_out, not_188_out, not_189_out, not_190_out, not_191_out, not_192_out, not_193_out,
       not_194_out, not_195_out, not_196_out, not_197_out, not_198_out, not_199_out, not_200_out,
       not_201_out, not_202_out, not_203_out, not_204_out, not_205_out, not_206_out;

  not not_1 (not_1_out, Op3);
  and and_1 (RegDst, not_1_out, not_2_out);
  not not_2 (not_2_out, Op1);
  not not_3 (not_3_out, Op5);
  and and_2 (and_2_out, not_3_out, Op0);
  not not_4 (not_4_out, Op3);
  and and_3 (and_3_out, not_4_out, Op0);
  and and_4 (and_4_out, Op3, not_5_out);
  not not_5 (not_5_out, Op1);
  and and_5 (and_5_out, Op3, not_6_out);
  not not_6 (not_6_out, Op0);
  and and_6 (and_6_out, Op3, not_7_out);
  not not_7 (not_7_out, Fun0);
  and and_7 (and_7_out, Op3, Fun1);
  and and_8 (and_8_out, Op3, Fun2);
  and and_9 (and_9_out, Op3, Fun3);
  and and_10 (and_10_out, Op3, Fun4);
  and and_11 (and_11_out, Op3, Fun5);
  and and_12 (and_12_out, Op3, Op2);
  and and_13 (and_13_out, Op4, Op0);
  not not_8 (not_8_out, Op4);
  not not_9 (not_9_out, Op2);
  not not_10 (not_10_out, Op0);
  not not_11 (not_11_out, Fun5);
  not not_12 (not_12_out, Fun4);
  not not_13 (not_13_out, Fun2);
  not not_14 (not_14_out, Fun1);
  not not_15 (not_15_out, Op1);
  not not_16 (not_16_out, Op0);
  not not_17 (not_17_out, Fun5);
  not not_18 (not_18_out, Fun4);
  not not_19 (not_19_out, Fun3);
  not not_20 (not_20_out, Fun2);
  not not_21 (not_21_out, Fun1);
  not not_22 (not_22_out, Fun0);
  not not_23 (not_23_out, Op3);
  not not_24 (not_24_out, Fun5);
  not not_25 (not_25_out, Fun4);
  not not_26 (not_26_out, Fun3);
  not not_27 (not_27_out, Fun5);
  not not_28 (not_28_out, Fun4);
  not not_29 (not_29_out, Fun2);
  not not_30 (not_30_out, Fun0);
  not not_31 (not_31_out, Fun5);
  not not_32 (not_32_out, Fun4);
  not not_33 (not_33_out, Fun3);
  not not_34 (not_34_out, Fun2);
  not not_35 (not_35_out, Fun1);
  not not_36 (not_36_out, Op5);
  not not_37 (not_37_out, Op2);
  not not_38 (not_38_out, Fun4);
  not not_39 (not_39_out, Fun3);
  not not_40 (not_40_out, Fun2);
  not not_41 (not_41_out, Fun0);
  not not_42 (not_42_out, Op5);
  not not_43 (not_43_out, Op2);
  not not_44 (not_44_out, Fun4);
  not not_45 (not_45_out, Fun2);
  not not_46 (not_46_out, Fun0);
  not not_47 (not_47_out, Op5);
  not not_48 (not_48_out, Op2);
  not not_49 (not_49_out, Fun4);
  not not_50 (not_50_out, Fun3);
  not not_51 (not_51_out, Fun1);
  not not_52 (not_52_out, Op5);
  not not_53 (not_53_out, Op2);
  not not_54 (not_54_out, Op3);
  not not_55 (not_55_out, Op2);
  not not_56 (not_56_out, Op4);
  not not_57 (not_57_out, Op2);
  not not_58 (not_58_out, Op4);
  not not_59 (not_59_out, Op2);
  not not_60 (not_60_out, Fun3);
  not not_61 (not_61_out, Op4);
  not not_62 (not_62_out, Op2);
  not not_63 (not_63_out, Op4);
  not not_64 (not_64_out, Op2);
  not not_65 (not_65_out, Fun1);
  not not_66 (not_66_out, Op4);
  not not_67 (not_67_out, Op2);
  not not_68 (not_68_out, Op4);
  not not_69 (not_69_out, Op2);
  not not_70 (not_70_out, Op5);
  not not_71 (not_71_out, Op5);
  not not_72 (not_72_out, Op2);
  not not_73 (not_73_out, Op3);
  not not_74 (not_74_out, Op2);
  not not_75 (not_75_out, Op5);
  not not_76 (not_76_out, Op3);
  not not_77 (not_77_out, Op3);
  not not_78 (not_78_out, Op1);
  not not_79 (not_79_out, Op3);
  not not_80 (not_80_out, Fun5);
  not not_81 (not_81_out, Fun4);
  not not_82 (not_82_out, Fun3);
  not not_83 (not_83_out, Fun2);
  not not_84 (not_84_out, Fun1);
  not not_85 (not_85_out, Fun0);
  not not_86 (not_86_out, Op3);
  not not_87 (not_87_out, Fun5);
  not not_88 (not_88_out, Fun4);
  not not_89 (not_89_out, Fun3);
  not not_90 (not_90_out, Op3);
  not not_91 (not_91_out, Fun5);
  not not_92 (not_92_out, Fun4);
  not not_93 (not_93_out, Fun2);
  not not_94 (not_94_out, Fun0);
  not not_95 (not_95_out, Op3);
  not not_96 (not_96_out, Op3);
  not not_97 (not_97_out, Op4);
  not not_98 (not_98_out, Op2);
  not not_99 (not_99_out, Op0);
  not not_100 (not_100_out, Fun5);
  not not_101 (not_101_out, Fun4);
  not not_102 (not_102_out, Fun2);
  not not_103 (not_103_out, Fun1);
  not not_104 (not_104_out, Op1);
  not not_105 (not_105_out, Op0);
  not not_106 (not_106_out, Fun0);
  not not_107 (not_107_out, Op3);
  not not_108 (not_108_out, Op4);
  not not_109 (not_109_out, Op2);
  not not_110 (not_110_out, Fun5);
  not not_111 (not_111_out, Fun4);
  not not_112 (not_112_out, Fun3);
  not not_113 (not_113_out, Fun2);
  not not_114 (not_114_out, Fun1);
  not not_115 (not_115_out, Op5);
  not not_116 (not_116_out, Op4);
  not not_117 (not_117_out, Op3);
  not not_118 (not_118_out, Op2);
  not not_119 (not_119_out, Op5);
  not not_120 (not_120_out, Op4);
  not not_121 (not_121_out, Op2);
  not not_122 (not_122_out, Op1);
  not not_123 (not_123_out, Op5);
  not not_124 (not_124_out, Op4);
  not not_125 (not_125_out, Op3);
  not not_126 (not_126_out, Op2);
  not not_127 (not_127_out, Op1);
  not not_128 (not_128_out, Op0);
  not not_129 (not_129_out, Fun5);
  not not_130 (not_130_out, Fun4);
  not not_131 (not_131_out, Fun3);
  not not_132 (not_132_out, Fun2);
  not not_133 (not_133_out, Fun0);
  not not_134 (not_134_out, Op5);
  not not_135 (not_135_out, Op4);
  not not_136 (not_136_out, Op3);
  not not_137 (not_137_out, Op2);
  not not_138 (not_138_out, Op1);
  not not_139 (not_139_out, Op0);
  not not_140 (not_140_out, Fun4);
  not not_141 (not_141_out, Fun2);
  not not_142 (not_142_out, Fun0);
  not not_143 (not_143_out, Op5);
  not not_144 (not_144_out, Op4);
  not not_145 (not_145_out, Op2);
  not not_146 (not_146_out, Op0);
  not not_147 (not_147_out, Fun5);
  not not_148 (not_148_out, Fun4);
  not not_149 (not_149_out, Fun2);
  not not_150 (not_150_out, Fun1);
  not not_151 (not_151_out, Op2);
  not not_152 (not_152_out, Fun3);
  and and_14 (and_14_out, not_151_out, not_152_out, Fun0);
  not not_153 (not_153_out, Fun5);
  and and_15 (and_15_out, not_153_out, Fun1);
  not not_154 (not_154_out, Fun5);
  and and_16 (and_16_out, not_154_out, Fun2);
  and and_17 (and_17_out, Fun2, Fun1);
  not not_155 (not_155_out, Op1);
  and and_18 (and_18_out, not_155_out, Fun3, not_156_out);
  not not_156 (not_156_out, Fun1);
  not not_157 (not_157_out, Fun2);
  and and_19 (and_19_out, Fun5, not_157_out, not_158_out);
  not not_158 (not_158_out, Fun1);
  and and_20 (and_20_out, Fun5, Fun0);
  not not_159 (not_159_out, Op3);
  and and_21 (and_21_out, not_159_out, Op1);
  not not_160 (not_160_out, Op3);
  and and_22 (and_22_out, not_160_out, Op2);
  and and_23 (and_23_out, Op2, Op1);
  and and_24 (and_24_out, Op3, not_161_out);
  not not_161 (not_161_out, Fun0);
  not not_162 (not_162_out, Op5);
  not not_163 (not_163_out, Op4);
  not not_164 (not_164_out, Op3);
  not not_165 (not_165_out, Op2);
  not not_166 (not_166_out, Op1);
  not not_167 (not_167_out, Op0);
  not not_168 (not_168_out, Fun5);
  not not_169 (not_169_out, Fun4);
  not not_170 (not_170_out, Fun3);
  not not_171 (not_171_out, Fun2);
  not not_172 (not_172_out, Fun1);
  not not_173 (not_173_out, Fun0);
  not not_174 (not_174_out, Op5);
  not not_175 (not_175_out, Op4);
  not not_176 (not_176_out, Op3);
  not not_177 (not_177_out, Op2);
  not not_178 (not_178_out, Op1);
  not not_179 (not_179_out, Op0);
  not not_180 (not_180_out, Fun4);
  not not_181 (not_181_out, Fun3);
  not not_182 (not_182_out, Fun1);
  not not_183 (not_183_out, Op5);
  not not_184 (not_184_out, Op4);
  not not_185 (not_185_out, Op1);
  not not_186 (not_186_out, Op0);
  not not_187 (not_187_out, Fun5);
  not not_188 (not_188_out, Fun4);
  not not_189 (not_189_out, Fun3);
  not not_190 (not_190_out, Fun2);
  not not_191 (not_191_out, Fun1);
  not not_192 (not_192_out, Op5);
  not not_193 (not_193_out, Op4);
  not not_194 (not_194_out, Op1);
  not not_195 (not_195_out, Fun5);
  not not_196 (not_196_out, Fun4);
  not not_197 (not_197_out, Fun3);
  not not_198 (not_198_out, Fun2);
  not not_199 (not_199_out, Op5);
  not not_200 (not_200_out, Op4);
  not not_201 (not_201_out, Op1);
  not not_202 (not_202_out, Fun5);
  not not_203 (not_203_out, Fun4);
  not not_204 (not_204_out, Fun3);
  not not_205 (not_205_out, Fun1);
  not not_206 (not_206_out, Fun0);
  and and_25 (and_25_out, not_8_out, Op3, not_9_out, Op1, not_10_out, not_11_out, not_12_out, Fun3, not_13_out, not_14_out, Fun0);
  and and_26 (and_26_out, Op5, not_15_out);
  and and_27 (and_27_out, Op5, not_16_out);
  and and_28 (and_28_out, Op5, not_17_out, not_18_out, not_19_out, not_20_out, not_21_out, not_22_out);
  and and_29 (and_29_out, Op5, not_23_out, not_24_out, not_25_out, not_26_out, Fun2, Fun1, Fun0);
  and and_30 (and_30_out, Op5, not_27_out, not_28_out, Fun3, not_29_out, Fun1, not_30_out);
  and and_31 (and_31_out, Op5, Op2);
  and and_32 (and_32_out, Op5, Op3, not_31_out, not_32_out, not_33_out, not_34_out, not_35_out);
  and and_33 (and_33_out, Op5, Op4);
  and and_34 (and_34_out, not_36_out, not_37_out, not_38_out, not_39_out, not_40_out, not_41_out);
  and and_35 (and_35_out, not_42_out, not_43_out, Fun5, not_44_out, not_45_out, Fun1, not_46_out);
  and and_36 (and_36_out, not_47_out, not_48_out, Fun5, not_49_out, not_50_out, Fun2, not_51_out);
  and and_37 (and_37_out, not_52_out, not_53_out, Op0);
  and and_38 (and_38_out, not_54_out, not_55_out, Op1);
  and and_39 (and_39_out, not_56_out, not_57_out, Op1, Op0, Fun0);
  and and_40 (and_40_out, not_58_out, not_59_out, Op1, Op0, not_60_out, Fun1);
  and and_41 (and_41_out, not_61_out, not_62_out, Op1, Op0, Fun2);
  and and_42 (and_42_out, not_63_out, not_64_out, Op1, Op0, Fun3, not_65_out);
  and and_43 (and_43_out, not_66_out, not_67_out, Op1, Op0, Fun4);
  and and_44 (and_44_out, not_68_out, not_69_out, Op1, Op0, Fun5);
  and and_45 (and_45_out, not_70_out, Op3);
  and and_46 (and_46_out, not_71_out, Op4, not_72_out);
  and and_47 (and_47_out, Op5, not_73_out, not_74_out);
  and and_48 (and_48_out, not_75_out, not_76_out, Op0);
  and and_49 (and_49_out, not_77_out, not_78_out, Op0);
  and and_50 (and_50_out, not_79_out, Op0, not_80_out, not_81_out, not_82_out, not_83_out, not_84_out, not_85_out);
  and and_51 (and_51_out, not_86_out, Op0, not_87_out, not_88_out, not_89_out, Fun2, Fun1, Fun0);
  and and_52 (and_52_out, not_90_out, Op0, not_91_out, not_92_out, Fun3, not_93_out, Fun1, not_94_out);
  and and_53 (and_53_out, not_95_out, Op2, Op0);
  and and_54 (and_54_out, Op4, not_96_out, Op0);
  and and_55 (and_55_out, not_97_out, Op3, not_98_out, Op1, not_99_out, not_100_out, not_101_out, Fun3, not_102_out, not_103_out, Fun0);
  and and_56 (and_56_out, Op5, Op3, not_104_out);
  and and_57 (and_57_out, Op5, Op3, not_105_out);
  and and_58 (and_58_out, Op5, Op3, not_106_out);
  and and_59 (and_59_out, Op5, Op3, Fun1);
  and and_60 (and_60_out, Op5, Op3, Fun2);
  and and_61 (and_61_out, Op5, Op3, Fun3);
  and and_62 (and_62_out, Op5, Op3, Fun4);
  and and_63 (and_63_out, Op5, Op3, Fun5);
  and and_64 (and_64_out, Op5, Op3, Op2);
  and and_65 (and_65_out, Op5, Op4, Op3);
  and and_66 (and_66_out, not_107_out, Op2);
  and and_67 (and_67_out, Op5, not_108_out, Op3, not_109_out, Op1, Op0, not_110_out, not_111_out, not_112_out, not_113_out, not_114_out, Fun0);
  and and_68 (and_68_out, not_115_out, not_116_out, not_117_out, not_118_out, Op1);
  and and_69 (and_69_out, not_119_out, not_120_out, Op3, not_121_out, not_122_out, Op0);
  and and_70 (and_70_out, not_123_out, not_124_out, not_125_out, not_126_out, not_127_out, not_128_out, not_129_out, not_130_out, not_131_out, not_132_out, not_133_out);
  and and_71 (and_71_out, not_134_out, not_135_out, not_136_out, not_137_out, not_138_out, not_139_out, Fun5, not_140_out, Fun3, not_141_out, Fun1, not_142_out);
  and and_72 (and_72_out, not_143_out, not_144_out, Op3, not_145_out, Op1, not_146_out, not_147_out, not_148_out, Fun3, not_149_out, not_150_out, Fun0);
  and and_73 (and_73_out, not_162_out, not_163_out, not_164_out, not_165_out, not_166_out, not_167_out, not_168_out, not_169_out, not_170_out, not_171_out, not_172_out, not_173_out);
  and and_74 (and_74_out, not_174_out, not_175_out, not_176_out, not_177_out, not_178_out, not_179_out, Fun5, not_180_out, not_181_out, Fun2, not_182_out);
  and and_75 (and_75_out, not_183_out, not_184_out, Op3, Op2, not_185_out, not_186_out, not_187_out, not_188_out, not_189_out, not_190_out, not_191_out, Fun0);
  and and_76 (and_76_out, not_192_out, not_193_out, Op3, Op2, not_194_out, Op0, not_195_out, not_196_out, not_197_out, not_198_out, Fun1, Fun0);
  and and_77 (and_77_out, not_199_out, not_200_out, Op3, Op2, not_201_out, Op0, not_202_out, not_203_out, not_204_out, Fun2, not_205_out, not_206_out);
  or or_1 (AlUSrc, and_2_out, and_3_out, and_4_out, and_5_out, and_6_out, and_7_out, and_8_out, and_9_out, and_10_out, and_11_out, and_12_out, and_13_out);
  or or_2 (MemtoReg, and_25_out, and_26_out, and_27_out, and_28_out, and_29_out, and_30_out, and_31_out, and_32_out, and_33_out);
  or or_3 (RegWrite, and_34_out, and_35_out, and_36_out, and_37_out, and_38_out, and_39_out, and_40_out, and_41_out, and_42_out, and_43_out, and_44_out, and_45_out, and_46_out, and_47_out);
  or or_4 (MemRead, and_48_out, and_49_out, and_50_out, and_51_out, and_52_out, and_53_out, and_54_out);
  or or_5 (MemWrite, and_55_out, and_56_out, and_57_out, and_58_out, and_59_out, and_60_out, and_61_out, and_62_out, and_63_out, and_64_out, and_65_out);
  or or_6 (Branch, and_66_out, and_67_out);
  or or_7 (Jump, and_68_out, and_69_out);
  or or_8 (AluCtr0, and_70_out, and_71_out, and_72_out);
  or or_9 (AluCtr1, and_14_out, and_15_out, and_16_out, and_17_out, and_18_out, Fun4, and_19_out, and_20_out, Op0, and_21_out, and_22_out, and_23_out, and_24_out, Op4, Op5);
  or or_10 (AluCtr2, and_73_out, and_74_out, and_75_out, and_76_out, and_77_out);
endmodule

module Forward (
  input  MEM_WB_RegWrite,
  input  EX_MEM_RegWrite,
  input  [4:0] EX_MEM_Rd,
  input  [4:0] MEM_WB_Rd,
  input  [4:0] ID_EX_Rs,
  input  [4:0] ID_EX_Rt,
  output [1:0] ForwardA,
  output [1:0] ForwardB
);

  wire comparator_1_gt, comparator_1_lt, comparator_2_eq, comparator_3_gt, comparator_3_lt, comparator_4_eq,
       comparator_5_gt, comparator_5_lt, comparator_6_eq, comparator_7_gt, comparator_7_lt, comparator_8_eq,
       ForwardA_01, ForwardA_10, ForwardB_01, ForwardB_10, or_1_out, or_2_out, or_3_out, or_4_out;
  wire [1:0] multiplexer_1_out, multiplexer_2_out;

  Comparator #(.width(5), .mode("unsigned")) comparator_1 (
    .a(EX_MEM_Rd), .b({5{1'b0}}), .gt(comparator_1_gt), .lt(comparator_1_lt));  // open: eq
  Comparator #(.width(5), .mode("unsigned")) comparator_2 (
    .a(EX_MEM_Rd), .b(ID_EX_Rs), .eq(comparator_2_eq));  // open: gt, lt
  Comparator #(.width(5), .mode("unsigned")) comparator_3 (
    .a(EX_MEM_Rd), .b({5{1'b0}}), .gt(comparator_3_gt), .lt(comparator_3_lt));  // open: eq
  Comparator #(.width(5), .mode("unsigned")) comparator_4 (
    .a(EX_MEM_Rd), .b(ID_EX_Rt), .eq(comparator_4_eq));  // open: gt, lt
  or or_1 (or_1_out, comparator_1_gt, comparator_1_lt);
  or or_2 (or_2_out, comparator_3_gt, comparator_3_lt);
  and and_1 (ForwardA_10, EX_MEM_RegWrite, or_1_out, comparator_2_eq);
  and and_2 (ForwardB_10, EX_MEM_RegWrite, or_2_out, comparator_4_eq);
  Multiplexer #(.width(2), .enable("false")) multiplexer_1 (
    .in0(2'b00), .in1(2'b10), .out(multiplexer_1_out), .sel(ForwardA_10));
  Multiplexer #(.width(2), .enable("false")) multiplexer_2 (
    .in0(2'b00), .in1(2'b10), .out(multiplexer_2_out), .sel(ForwardB_10));
  Multiplexer #(.width(2), .enable("false")) multiplexer_3 (
    .in0(multiplexer_1_out), .in1(2'b01), .out(ForwardA), .sel(ForwardA_01));
  Multiplexer #(.width(2), .enable("false")) multiplexer_4 (
    .in0(multiplexer_2_out), .in1(2'b01), .out(ForwardB), .sel(ForwardB_01));
  Comparator #(.width(5), .mode("unsigned")) comparator_5 (
    .a(MEM_WB_Rd), .b({5{1'b0}}), .gt(comparator_5_gt), .lt(comparator_5_lt));  // open: eq
  or or_3 (or_3_out, comparator_5_gt, comparator_5_lt);
  Comparator #(.width(5), .mode("unsigned")) comparator_6 (
    .a(MEM_WB_Rd), .b(ID_EX_Rs), .eq(comparator_6_eq));  // open: gt, lt
  Comparator #(.width(5), .mode("unsigned")) comparator_7 (
    .a(MEM_WB_Rd), .b({5{1'b0}}), .gt(comparator_7_gt), .lt(comparator_7_lt));  // open: eq
  Comparator #(.width(5), .mode("unsigned")) comparator_8 (
    .a(MEM_WB_Rd), .b(ID_EX_Rt), .eq(comparator_8_eq));  // open: gt, lt
  or or_4 (or_4_out, comparator_7_gt, comparator_7_lt);
  and and_3 (ForwardA_01, MEM_WB_RegWrite, or_3_out, comparator_6_eq, ~ForwardA_10);  // AND_Gate
  and and_4 (ForwardB_01, MEM_WB_RegWrite, or_4_out, comparator_8_eq, ~ForwardB_10);  // AND_Gate

  // Notes on the sheet:
  //   EX Hazard
  //   MEM Hazard
endmodule

module Stall (
  input  ID_EX_MemRead,
  input  stall,
  input  [4:0] ID_EX_Rt,
  input  [4:0] IF_ID_Rs,
  input  [4:0] IF_ID_Rt,
  input  [5:0] Opcode
);

  wire and_1_out, comparator_1_eq, comparator_2_eq, comparator_3_eq, or_1_out;

  Comparator #(.width(5), .mode("unsigned")) comparator_1 (
    .a(ID_EX_Rt), .b(IF_ID_Rs), .eq(comparator_1_eq));  // open: gt, lt
  Comparator #(.width(5), .mode("unsigned")) comparator_2 (
    .a(ID_EX_Rt), .b(IF_ID_Rt), .eq(comparator_2_eq));  // open: gt, lt
  Comparator #(.width(6), .mode("unsigned")) comparator_3 (
    .a(6'b101011), .b(Opcode), .eq(comparator_3_eq));  // open: gt, lt
  or or_1 (or_1_out, comparator_1_eq, comparator_2_eq);
  and and_1 (and_1_out, or_1_out, ~comparator_3_eq);  // AND_Gate
  and and_2 (stall, ID_EX_MemRead, and_1_out);
endmodule
