// Logisim project SingleCycleMips-Finished-Increment fixed.circ as structural Verilog: 7 circuits, main circuit main
module main (
  output [15:0] out_1,
  output [31:0] out_2,
  output [31:0] out_3,
  output [31:0] out_4,
  output [29:0] out_5,
  output [31:0] out_6
);

  wire alu_1_zero, and_1_out, Branch, clock_1_out, controltest8_1_aluop0, controltest8_1_aluop1,
       controltest8_1_alusrc, controltest8_1_memread, controltest8_1_memtoreg, controltest8_1_regdst, Jal,
       MemWr, WrReg;
  wire [1:0] PC;
  wire [2:0] alucontrol8_1_oper0;
  wire [3:0] adder_1_out;
  wire [4:0] WrAddr;
  wire [7:0] bit_extender_2_out, bit_extender_4_out;
  wire [27:0] adder_1_out_2, bit_extender_1_out, shifter_1_out;
  wire [31:0] adder_2_out, bit_extender_3_out, MemData, multiplexer_1_out, multiplexer_2_out,
       multiplexer_5_out, shifter_2_out, WrData;

  Clock clock_1 (.out(clock_1_out));
  assign bit_extender_1_out = {{2{1'b0}}, {out_6[25:16], out_1}};  // Bit_Extender bit_extender_1
  Shifter #(.width(28)) shifter_1 (.in(bit_extender_1_out), .\dist (5'b00010), .out(shifter_1_out));
  Register #(.width(32)) u_PC (.D(multiplexer_1_out), .Q({out_5, PC}), .clk(clock_1_out));  // open: en, clr
  Adder #(.width(32)) adder_1 (.a(32'h4), .b({out_5, PC}), .out({adder_1_out, adder_1_out_2}));  // open: cin, cout
  Multiplexer #(.width(32), .enable("false")) multiplexer_1 (
    .in0(multiplexer_2_out), .in1({adder_1_out, shifter_1_out}), .out(multiplexer_1_out), .sel(Jal));
  Bit_Extender #(.in_width(30), .out_width(8)) bit_extender_2 (.in(out_5), .out(bit_extender_2_out));
  Multiplexer #(.width(32), .enable("false")) multiplexer_2 (
    .in0({adder_1_out, adder_1_out_2}), .in1(adder_2_out), .out(multiplexer_2_out), .sel(and_1_out));
  ROM #(.dataWidth(32)) rom_1 (.addr(bit_extender_2_out), .data({out_6[31:16], out_1}));  // open: sel
  assign bit_extender_3_out = {{16{1'b0}}, out_1};  // Bit_Extender bit_extender_3
  and and_1 (and_1_out, Branch, alu_1_zero);
  Multiplexer #(.width(5), .enable("false")) multiplexer_3 (
    .in0(out_6[20:16]), .in1(out_1[15:11]), .out(WrAddr), .sel(controltest8_1_regdst));
  ControlTest8 controltest8_1 (
    .Op5(out_6[31]), .Op4(out_6[30]), .Op3(out_6[29]), .Op2(out_6[28]), .Op1(out_6[27]), .Op0(out_6[26]),
    .RegDst(controltest8_1_regdst), .AlUSrc(controltest8_1_alusrc), .MemtoReg(controltest8_1_memtoreg),
    .RegWrite(WrReg), .MemRead(controltest8_1_memread), .MemWrite(MemWr), .Branch(Branch),
    .ALUOp1(controltest8_1_aluop1), .AlUOp0(controltest8_1_aluop0), .Jump(Jal));
  Shifter #(.width(32)) shifter_2 (.in(bit_extender_3_out), .\dist (5'b00010), .out(shifter_2_out));
  Adder #(.width(32)) adder_2 (
    .a({adder_1_out, adder_1_out_2}), .b(shifter_2_out), .out(adder_2_out));  // open: cin, cout
  Multiplexer #(.width(32), .enable("false")) multiplexer_4 (
    .in0(out_3), .in1(out_4), .out(WrData), .sel(controltest8_1_memtoreg));
  RegFile regfile_1 (
    .WrAddr(WrAddr), .WrData(WrData), .WrReg(WrReg), .RdAddr1(out_6[25:21]), .RdAddr2(out_6[20:16]),
    .RdData1(out_2), .RdData2(MemData), .Clock(clock_1_out));  // open: out_7, out_8
  Multiplexer #(.width(32), .enable("false")) multiplexer_5 (
    .in0(MemData), .in1(bit_extender_3_out), .out(multiplexer_5_out), .sel(controltest8_1_alusrc));
  ALUControl8 alucontrol8_1 (
    .ALU1(controltest8_1_aluop1), .ALU0(controltest8_1_aluop0), .F3(out_1[3]), .F2(out_1[2]), .F1(out_1[1]),
    .F0(out_1[0]), .Oper2(alucontrol8_1_oper0[2]), .Oper1(alucontrol8_1_oper0[1]),
    .Oper0(alucontrol8_1_oper0[0]));
  ALU alu_1 (
    .ALUCtl(alucontrol8_1_oper0), .A(out_2), .B(multiplexer_5_out), .ALUResult(out_3), .Zero(alu_1_zero),
    .Shamt({5{1'b0}}));  // open: Overflow
  Bit_Extender #(.in_width(32), .out_width(8)) bit_extender_4 (.in(out_3), .out(bit_extender_4_out));
  RAM #(.dataWidth(32), .bus("separate")) ram_1 (
    .addr(bit_extender_4_out), .din(MemData), .data(out_4), .str(MemWr), .clk(clock_1_out),
    .ld(controltest8_1_memread));  // open: sel, clr
  // Probe on {out_5, PC}
  // Probe on Branch
  // Probe on Jal
  // Probe on Jal
  // Probe on Jal
  // Probe on WrReg
  // Probe on WrAddr
  // Probe on WrData
  // Probe on MemWr
  // Probe on MemData

  assign out_6[15:0] = out_1;

  // Other names for the same wires on the sheet: Jr = Jal; Jump = Jal; _0 = out_1[0]; _1 = out_1[1]; _2 = out_1[2];
  //   _3 = out_1[3]; _4 = out_1[4]; _7 = out_1[7]; _8 = out_1[8]; _9 = out_1[9]; PC[31:2] = out_5

  // Notes on the sheet:
  //   JUMP
  //   contents of rom_1 (hex, n*v repeats v):
  //   20010008 0 0 0 34220005 0 0 0 3043ffff 0 0 0 612020 0 0 0 832822 0 0 0 223024 0 0 0 c33825 0 0 0
  //   aca40064 0 0 0 8ca80064 0 0 0 22482a 0 0 0 282a0005 0 0 0 11050003 0 0 0 1034022 0 0 0 c00000b 0 0 0
  //   200b0001 0 0 0 200c0005
  //   ALUSrc
  //   MemtoReg
  //   Branch
endmodule

module _32bit (
  input  Add_Sub_control,
  input  [31:0] in_2,
  input  [31:0] in_3,
  output [31:0] out_4,
  output carry_out
);

  wire adder_1_cout, subtractor_1_bout;
  wire [31:0] adder_1_out, subtractor_1_out;

  Adder #(.width(32)) adder_1 (.a(in_2), .b(in_3), .out(adder_1_out), .cout(adder_1_cout));  // open: cin
  Subtractor #(.width(32)) subtractor_1 (
    .a(in_2), .b(in_3), .out(subtractor_1_out), .bout(subtractor_1_bout));  // open: bin
  Multiplexer #(.width(32), .enable("false")) multiplexer_1 (
    .in0(adder_1_out), .in1(subtractor_1_out), .out(out_4), .sel(Add_Sub_control));
  Multiplexer #(.enable("false")) multiplexer_2 (
    .in0(adder_1_cout), .in1(subtractor_1_bout), .out(carry_out), .sel(Add_Sub_control));
endmodule

module ALU (
  input  [2:0] ALUCtl,
  input  [31:0] A,
  input  [31:0] B,
  input  [4:0] Shamt,
  output [31:0] ALUResult,
  output Zero,
  output Overflow
);

  wire and_2_out, and_3_out, comparator_1_lt, not_1_out, not_2_out, not_3_out, or_2_out;
  wire [31:0] Add, And, LessThan, Or, ShiftLeft, ShiftRight, Sub, Xor;

  Adder #(.width(32)) adder_1 (.a(A), .b(B), .out(Add));  // open: cin, cout
  Subtractor #(.width(32)) subtractor_1 (.a(A), .b(B), .out(Sub));  // open: bin, bout
  assign And = A & B;  // AND_Gate and_1, 32 bits wide
  assign Or = A | B;  // OR_Gate or_1, 32 bits wide
  assign Xor = A ^ B;  // XOR_Gate xor_1, 32 bits wide
  Comparator #(.width(32)) comparator_1 (.a(A), .b(B), .lt(comparator_1_lt));  // open: gt, eq
  assign LessThan = {{31{1'b0}}, comparator_1_lt};  // Bit_Extender bit_extender_1
  Shifter #(.width(32)) shifter_1 (.in(B), .\dist (Shamt), .out(ShiftLeft));
  Shifter #(.width(32), .shift("lr")) shifter_2 (.in(B), .\dist (Shamt), .out(ShiftRight));
  Multiplexer #(.select(3), .width(32), .enable("false")) multiplexer_1 (
    .in0(Sub), .in1(And), .in2(Add), .in3(Or), .in4(LessThan), .in5(Xor), .in6(ShiftLeft), .in7(ShiftRight),
    .out(ALUResult), .sel(ALUCtl));
  not not_1 (not_1_out, ALUCtl[0]);
  not not_2 (not_2_out, ALUCtl[1]);
  not not_3 (not_3_out, ALUCtl[2]);
  and and_2 (and_2_out, not_1_out, not_2_out, not_3_out);
  and and_3 (and_3_out, not_1_out, not_2_out, ALUCtl[2]);
  Overflow overflow_1 (
    .Add(and_2_out), .Sub(and_3_out), .ASign(A[31]), .BSign(B[31]), .ResultSign(ALUResult[31]),
    .Overflow(Overflow));
  or or_2 (or_2_out, ALUResult[0], ALUResult[1], ALUResult[2], ALUResult[3], ALUResult[4], ALUResult[5], ALUResult[6], ALUResult[7], ALUResult[8], ALUResult[9], ALUResult[10], ALUResult[11], ALUResult[12], ALUResult[13], ALUResult[14], ALUResult[15], ALUResult[16], ALUResult[17], ALUResult[18], ALUResult[19], ALUResult[20], ALUResult[21], ALUResult[22], ALUResult[23], ALUResult[24], ALUResult[25], ALUResult[26], ALUResult[27], ALUResult[28], ALUResult[29], ALUResult[30], ALUResult[31]);
  not not_4 (Zero, or_2_out);

  // Other names for the same wires on the sheet: ASign = A[31]; ResultSign = ALUResult[31]; BSign = B[31]
endmodule

module RegFile (
  input  [4:0] WrAddr,
  input  [31:0] WrData,
  input  WrReg,
  input  [4:0] RdAddr1,
  input  [4:0] RdAddr2,
  input  Clock,
  output [31:0] out_7,
  output [31:0] out_8,
  output [31:0] RdData1,
  output [31:0] RdData2
);

  wire WrReg0, WrReg1, WrReg2, WrReg3, WrReg4, WrReg5, WrReg6, WrReg7, WrReg8, WrReg9, WrReg10, WrReg11,
       WrReg12, WrReg13, WrReg14, WrReg15, WrReg16, WrReg17, WrReg18, WrReg19, WrReg20, WrReg21, WrReg22,
       WrReg23, WrReg24, WrReg25, WrReg26, WrReg27, WrReg28, WrReg29, WrReg30, WrReg31;
  wire [31:0] RegData2, RegData4, RegData5, RegData6, RegData7, RegData8, RegData9, RegData10, RegData11,
       RegData12, RegData13, RegData14, RegData15, RegData16, RegData17, RegData18, RegData19, RegData20,
       RegData21, RegData22, RegData23, RegData24, RegData25, RegData26, RegData27, RegData28, RegData29,
       RegData30, RegData31;

  Demultiplexer #(.select(5), .enable("false")) demultiplexer_1 (
    .out0(WrReg0), .out1(WrReg1), .out2(WrReg2), .out3(WrReg3), .out4(WrReg4), .out5(WrReg5), .out6(WrReg6),
    .out7(WrReg7), .out8(WrReg8), .out9(WrReg9), .out10(WrReg10), .out11(WrReg11), .out12(WrReg12),
    .out13(WrReg13), .out14(WrReg14), .out15(WrReg15), .out16(WrReg16), .out17(WrReg17), .out18(WrReg18),
    .out19(WrReg19), .out20(WrReg20), .out21(WrReg21), .out22(WrReg22), .out23(WrReg23), .out24(WrReg24),
    .out25(WrReg25), .out26(WrReg26), .out27(WrReg27), .out28(WrReg28), .out29(WrReg29), .out30(WrReg30),
    .out31(WrReg31), .in(WrReg), .sel(WrAddr));
  Register #(.width(32)) Reg4 (.D(WrData), .en(WrReg4), .Q(RegData4), .clk(Clock));  // open: clr
  Register #(.width(32)) Reg8 (.D(WrData), .en(WrReg8), .Q(RegData8), .clk(Clock));  // open: clr
  Register #(.width(32)) Reg12 (.D(WrData), .en(WrReg12), .Q(RegData12), .clk(Clock));  // open: clr
  Register #(.width(32)) Reg16 (.D(WrData), .en(WrReg16), .Q(RegData16), .clk(Clock));  // open: clr
  Register #(.width(32)) Reg20 (.D(WrData), .en(WrReg20), .Q(RegData20), .clk(Clock));  // open: clr
  Register #(.width(32)) Reg24 (.D(WrData), .en(WrReg24), .Q(RegData24), .clk(Clock));  // open: clr
  Register #(.width(32)) Reg28 (.D(WrData), .en(WrReg28), .Q(RegData28), .clk(Clock));  // open: clr
  Register #(.width(32)) Reg1 (.D(WrData), .en(WrReg1), .Q(out_7), .clk(Clock));  // open: clr
  Register #(.width(32)) Reg5 (.D(WrData), .en(WrReg5), .Q(RegData5), .clk(Clock));  // open: clr
  Register #(.width(32)) Reg9 (.D(WrData), .en(WrReg9), .Q(RegData9), .clk(Clock));  // open: clr
  Register #(.width(32)) Reg13 (.D(WrData), .en(WrReg13), .Q(RegData13), .clk(Clock));  // open: clr
  Register #(.width(32)) Reg17 (.D(WrData), .en(WrReg17), .Q(RegData17), .clk(Clock));  // open: clr
  Register #(.width(32)) Reg21 (.D(WrData), .en(WrReg21), .Q(RegData21), .clk(Clock));  // open: clr
  Register #(.width(32)) Reg25 (.D(WrData), .en(WrReg25), .Q(RegData25), .clk(Clock));  // open: clr
  Register #(.width(32)) Reg29 (.D(WrData), .en(WrReg29), .Q(RegData29), .clk(Clock));  // open: clr
  Register #(.width(32)) Reg2 (.D(WrData), .en(WrReg2), .Q(RegData2), .clk(Clock));  // open: clr
  Register #(.width(32)) Reg6 (.D(WrData), .en(WrReg6), .Q(RegData6), .clk(Clock));  // open: clr
  Register #(.width(32)) Reg10 (.D(WrData), .en(WrReg10), .Q(RegData10), .clk(Clock));  // open: clr
  Register #(.width(32)) Reg14 (.D(WrData), .en(WrReg14), .Q(RegData14), .clk(Clock));  // open: clr
  Register #(.width(32)) Reg18 (.D(WrData), .en(WrReg18), .Q(RegData18), .clk(Clock));  // open: clr
  Register #(.width(32)) Reg22 (.D(WrData), .en(WrReg22), .Q(RegData22), .clk(Clock));  // open: clr
  Register #(.width(32)) Reg26 (.D(WrData), .en(WrReg26), .Q(RegData26), .clk(Clock));  // open: clr
  Register #(.width(32)) Reg30 (.D(WrData), .en(WrReg30), .Q(RegData30), .clk(Clock));  // open: clr
  Register #(.width(32)) Reg3 (.D(WrData), .en(WrReg3), .Q(out_8), .clk(Clock));  // open: clr
  Register #(.width(32)) Reg7 (.D(WrData), .en(WrReg7), .Q(RegData7), .clk(Clock));  // open: clr
  Register #(.width(32)) Reg11 (.D(WrData), .en(WrReg11), .Q(RegData11), .clk(Clock));  // open: clr
  Register #(.width(32)) Reg15 (.D(WrData), .en(WrReg15), .Q(RegData15), .clk(Clock));  // open: clr
  Register #(.width(32)) Reg19 (.D(WrData), .en(WrReg19), .Q(RegData19), .clk(Clock));  // open: clr
  Register #(.width(32)) Reg23 (.D(WrData), .en(WrReg23), .Q(RegData23), .clk(Clock));  // open: clr
  Register #(.width(32)) Reg27 (.D(WrData), .en(WrReg27), .Q(RegData27), .clk(Clock));  // open: clr
  Register #(.width(32)) Reg31 (.D(WrData), .en(WrReg31), .Q(RegData31), .clk(Clock));  // open: clr
  Multiplexer #(.select(5), .width(32), .enable("false")) multiplexer_1 (
    .in0({32{1'b0}}), .in1(out_7), .in2(RegData2), .in3(out_8), .in4(RegData4), .in5(RegData5),
    .in6(RegData6), .in7(RegData7), .in8(RegData8), .in9(RegData9), .in10(RegData10), .in11(RegData11),
    .in12(RegData12), .in13(RegData13), .in14(RegData14), .in15(RegData15), .in16(RegData16),
    .in17(RegData17), .in18(RegData18), .in19(RegData19), .in20(RegData20), .in21(RegData21),
    .in22(RegData22), .in23(RegData23), .in24(RegData24), .in25(RegData25), .in26(RegData26),
    .in27(RegData27), .in28(RegData28), .in29(RegData29), .in30(RegData30), .in31(RegData31), .out(RdData1),
    .sel(RdAddr1));
  Multiplexer #(.select(5), .width(32), .enable("false")) multiplexer_2 (
    .in0({32{1'b0}}), .in1(out_7), .in2(RegData2), .in3(out_8), .in4(RegData4), .in5(RegData5),
    .in6(RegData6), .in7(RegData7), .in8(RegData8), .in9(RegData9), .in10(RegData10), .in11(RegData11),
    .in12(RegData12), .in13(RegData13), .in14(RegData14), .in15(RegData15), .in16(RegData16),
    .in17(RegData17), .in18(RegData18), .in19(RegData19), .in20(RegData20), .in21(RegData21),
    .in22(RegData22), .in23(RegData23), .in24(RegData24), .in25(RegData25), .in26(RegData26),
    .in27(RegData27), .in28(RegData28), .in29(RegData29), .in30(RegData30), .in31(RegData31), .out(RdData2),
    .sel(RdAddr2));

  // Other names for the same wires on the sheet: RegData1[31:0] = out_7; RegData3[31:0] = out_8
endmodule

module Overflow (
  input  Add,
  input  Sub,
  input  ASign,
  input  BSign,
  input  ResultSign,
  output Overflow
);

  wire and_1_out, and_2_out, or_1_out, xnor_1_out, xor_1_out, xor_2_out;

  xnor xnor_1 (xnor_1_out, ASign, BSign);
  xor xor_1 (xor_1_out, ASign, BSign);
  and and_1 (and_1_out, xnor_1_out, Add);
  and and_2 (and_2_out, xor_1_out, Sub);
  or or_1 (or_1_out, and_1_out, and_2_out);
  xor xor_2 (xor_2_out, ResultSign, ASign);
  and and_3 (Overflow, or_1_out, xor_2_out);

  // Notes on the sheet:
  //   Overflow occurs when doing addition and sign(A) == sign(B) && sign(result) != sign(A)
  //   Or
  //   Overflow occurs when doing subtraction and sign(A) != sign(B) && sign(result) != sign(A)
endmodule

module ControlTest8 (
  input  Op5,
  input  Op4,
  input  Op3,
  input  Op2,
  input  Op1,
  input  Op0,
  output RegDst,
  output AlUSrc,
  output MemtoReg,
  output RegWrite,
  output MemRead,
  output MemWrite,
  output Branch,
  output ALUOp1,
  output AlUOp0,
  output Jump
);

  wire and_3_out, and_4_out, and_6_out, and_7_out, and_8_out, and_9_out, and_10_out, and_11_out, and_12_out,
       and_13_out, and_14_out, and_15_out, not_1_out, not_2_out, not_3_out, not_4_out, not_5_out, not_6_out,
       not_7_out, not_8_out, not_9_out, not_10_out, not_11_out, not_12_out, not_13_out, not_14_out,
       not_15_out, not_16_out, not_17_out, not_18_out, not_19_out, not_20_out, not_21_out, not_22_out,
       not_23_out, not_24_out, not_25_out, not_26_out, not_27_out, not_28_out, not_29_out, not_30_out,
       not_31_out, not_32_out;

  not not_1 (not_1_out, Op3);
  not not_2 (not_2_out, Op1);
  or or_1 (AlUSrc, Op0, Op3);
  not not_3 (not_3_out, Op3);
  not not_4 (not_4_out, Op2);
  not not_5 (not_5_out, Op5);
  not not_6 (not_6_out, Op3);
  and and_1 (MemWrite, Op5, Op3);
  not not_7 (not_7_out, Op3);
  not not_8 (not_8_out, Op5);
  not not_9 (not_9_out, Op4);
  not not_10 (not_10_out, Op2);
  not not_11 (not_11_out, Op1);
  not not_12 (not_12_out, Op0);
  not not_13 (not_13_out, Op5);
  not not_14 (not_14_out, Op3);
  not not_15 (not_15_out, Op2);
  not not_16 (not_16_out, Op5);
  not not_17 (not_17_out, Op2);
  not not_18 (not_18_out, Op1);
  not not_19 (not_19_out, Op5);
  not not_20 (not_20_out, Op2);
  not not_21 (not_21_out, Op5);
  not not_22 (not_22_out, Op5);
  not not_23 (not_23_out, Op2);
  not not_24 (not_24_out, Op0);
  not not_25 (not_25_out, Op5);
  not not_26 (not_26_out, Op4);
  not not_27 (not_27_out, Op3);
  not not_28 (not_28_out, Op2);
  not not_29 (not_29_out, Op5);
  not not_30 (not_30_out, Op4);
  not not_31 (not_31_out, Op2);
  not not_32 (not_32_out, Op1);
  and and_2 (RegDst, not_1_out, not_2_out);
  and and_3 (and_3_out, not_3_out, not_4_out);
  and and_4 (and_4_out, not_5_out, Op3);
  and and_5 (MemRead, not_6_out, Op0);
  and and_6 (and_6_out, not_7_out, Op2);
  and and_7 (and_7_out, not_8_out, not_9_out, Op3, not_10_out, not_11_out, not_12_out);
  and and_8 (and_8_out, not_13_out, not_14_out, not_15_out);
  and and_9 (and_9_out, not_16_out, not_17_out, not_18_out);
  and and_10 (and_10_out, not_19_out, not_20_out, Op0);
  and and_11 (and_11_out, not_21_out, Op3, Op2);
  and and_12 (and_12_out, not_22_out, Op4, not_23_out);
  and and_13 (and_13_out, Op3, not_24_out);
  and and_14 (and_14_out, not_25_out, not_26_out, not_27_out, not_28_out, Op1);
  and and_15 (and_15_out, not_29_out, not_30_out, Op3, not_31_out, not_32_out, Op0);
  or or_2 (RegWrite, and_3_out, and_4_out);
  or or_3 (Branch, and_6_out, and_7_out);
  or or_4 (ALUOp1, and_8_out, and_9_out, and_10_out, and_11_out, and_12_out);
  or or_5 (AlUOp0, Op2, and_13_out);
  or or_6 (Jump, and_14_out, and_15_out);

  assign MemtoReg = Op5;
endmodule

module ALUControl8 (
  input  ALU1,
  input  ALU0,
  input  F3,
  input  F2,
  input  F1,
  input  F0,
  output Oper2,
  output Oper1,
  output Oper0
);

  wire and_2_out, and_3_out, and_4_out, and_5_out, and_6_out, and_7_out, and_8_out, and_9_out, and_10_out,
       and_11_out, and_12_out, not_1_out, not_2_out, not_3_out, not_4_out, not_5_out, not_6_out, not_7_out,
       not_8_out, not_9_out, not_10_out, not_11_out, not_12_out, not_13_out, not_14_out, not_15_out;

  not not_1 (not_1_out, ALU1);
  not not_2 (not_2_out, F3);
  not not_3 (not_3_out, F1);
  not not_4 (not_4_out, ALU0);
  not not_5 (not_5_out, F2);
  not not_6 (not_6_out, F1);
  not not_7 (not_7_out, F0);
  not not_8 (not_8_out, ALU1);
  not not_9 (not_9_out, ALU0);
  not not_10 (not_10_out, ALU0);
  not not_11 (not_11_out, F2);
  not not_12 (not_12_out, F1);
  not not_13 (not_13_out, F3);
  not not_14 (not_14_out, F2);
  not not_15 (not_15_out, F1);
  and and_1 (Oper0, ALU1, F2);
  and and_2 (and_2_out, not_1_out, ALU0, not_2_out, F2, not_3_out, F0);
  and and_3 (and_3_out, ALU1, not_4_out, F3);
  and and_4 (and_4_out, ALU1, F3, not_5_out);
  and and_5 (and_5_out, ALU1, F3, not_6_out);
  and and_6 (and_6_out, ALU1, F3, not_7_out);
  and and_7 (and_7_out, not_8_out, not_9_out);
  and and_8 (and_8_out, not_10_out, F0);
  and and_9 (and_9_out, ALU1, not_11_out, not_12_out);
  and and_10 (and_10_out, ALU1, not_13_out, F0);
  and and_11 (and_11_out, ALU1, not_14_out, F0);
  and and_12 (and_12_out, ALU1, not_15_out, F0);
  or or_1 (Oper2, and_2_out, and_3_out, and_4_out, and_5_out, and_6_out);
  or or_2 (Oper1, and_7_out, and_8_out, and_9_out, and_10_out, and_11_out, and_12_out);
endmodule
